// Digital circuit notS.dig as structural Verilog
module notS (
  input  In,
  output Out
);

  wire nfet_1_s;

  PullUp pullup_1 (.out(Out));
  NFET nfet_1 (.G(In), .D(Out), .S(nfet_1_s));
  NFET nfet_2 (.G(In), .D(nfet_1_s), .S(1'b0));
  NFET nfet_3 (.G(Out), .D(1'b1), .S(nfet_1_s));
endmodule
