// Digital circuit dffAopt.dig as structural Verilog
module dffAopt (
  input  D,
  input  C,
  input  R,
  input  S,
  output Q,
  output Q_2
);

  wire nfet_3_s, nfet_6_s, R_t, RESET, RESET_t, S_t, SET, SET_t;

  NFET nfet_1 (.G(R), .D(R_t), .S(1'b0));
  NFET nfet_2 (.G(S), .D(S_t), .S(1'b0));
  PullUp pullup_1 (.out(SET_t));
  s2 s2_1 (._1(SET), ._2(C), .D(SET_t), .S(R_t));
  PullUp pullup_2 (.out(RESET_t));
  NFET nfet_3 (.G(D), .D(RESET_t), .S(nfet_3_s));
  NFET nfet_4 (.G(Q), .D(Q_2), .S(nfet_3_s));
  NFET nfet_5 (.G(RESET), .D(nfet_3_s), .S(R_t));
  PullUp pullup_3 (.out(Q_2));
  PullUp pullup_4 (.out(RESET));
  s2 s2_2 (._1(C), ._2(RESET_t), .D(RESET), .S(nfet_6_s));
  PullUp pullup_5 (.out(SET));
  NFET nfet_6 (.G(RESET_t), .D(SET), .S(nfet_6_s));
  NFET nfet_7 (.G(SET_t), .D(nfet_6_s), .S(S_t));
  PullUp pullup_6 (.out(Q));
  NFET nfet_8 (.G(Q_2), .D(Q), .S(nfet_6_s));

  // Other names for the same wires on the sheet: Q_t = Q_2

  // Notes on the sheet:
  //   R: default 1
  //   S: default 1
endmodule
