// Digital circuit dffOpt.dig as structural Verilog
module dffOpt (
  input  D,
  input  C,
  output Q,
  output Q_2
);

  wire nfet_1_s, nfet_2_s, nfet_4_s, nfet_7_s, RESET, RESET_t, SET, SET_t;

  NFET nfet_1 (.G(RESET_t), .D(RESET), .S(nfet_1_s));
  NFET nfet_2 (.G(C), .D(nfet_1_s), .S(nfet_2_s));
  NFET nfet_3 (.G(SET_t), .D(nfet_2_s), .S(1'b0));
  PullUp pullup_1 (.out(RESET));
  PullUp pullup_2 (.out(RESET_t));
  NFET nfet_4 (.G(D), .D(RESET_t), .S(nfet_4_s));
  NFET nfet_5 (.G(RESET), .D(nfet_4_s), .S(1'b0));
  PullUp pullup_3 (.out(SET));
  NFET nfet_6 (.G(RESET_t), .D(SET), .S(nfet_2_s));
  PullUp pullup_4 (.out(SET_t));
  NFET nfet_7 (.G(SET), .D(SET_t), .S(nfet_7_s));
  NFET nfet_8 (.G(C), .D(nfet_7_s), .S(1'b0));
  PullUp pullup_5 (.out(Q));
  NFET nfet_9 (.G(Q_2), .D(Q), .S(nfet_2_s));
  PullUp pullup_6 (.out(Q_2));
  NFET nfet_10 (.G(Q), .D(Q_2), .S(nfet_4_s));

  // Other names for the same wires on the sheet: Q_t = Q_2
endmodule
