// Digital circuit dffRopt.dig as structural Verilog
module dffRopt (
  input  D,
  input  C,
  input  R,
  output Q,
  output Q_2
);

  wire nfet_2_s, nfet_3_s, nfet_5_s, nfet_7_s, nfet_9_s, nfet_11_s, nfet_13_s, R_t, RESET, RESET_t, SET,
       SET_t;

  NFET nfet_1 (.G(R), .D(R_t), .S(1'b0));
  PullUp pullup_1 (.out(RESET));
  NFET nfet_2 (.G(RESET_t), .D(RESET), .S(nfet_2_s));
  NFET nfet_3 (.G(SET_t), .D(nfet_2_s), .S(nfet_3_s));
  NFET nfet_4 (.G(C), .D(nfet_3_s), .S(1'b0));
  PullUp pullup_2 (.out(RESET_t));
  NFET nfet_5 (.G(RESET), .D(RESET_t), .S(nfet_5_s));
  NFET nfet_6 (.G(D), .D(nfet_5_s), .S(R_t));
  NFET nfet_7 (.G(SET_t), .D(SET), .S(nfet_7_s));
  NFET nfet_8 (.G(RESET_t), .D(nfet_7_s), .S(1'b0));
  PullUp pullup_3 (.out(SET));
  PullUp pullup_4 (.out(SET_t));
  NFET nfet_9 (.G(SET), .D(SET_t), .S(nfet_9_s));
  NFET nfet_10 (.G(C), .D(nfet_9_s), .S(R_t));
  NFET nfet_11 (.G(Q_2), .D(Q), .S(nfet_11_s));
  NFET nfet_12 (.G(SET_t), .D(nfet_11_s), .S(1'b0));
  PullUp pullup_5 (.out(Q));
  PullUp pullup_6 (.out(Q_2));
  NFET nfet_13 (.G(Q), .D(Q_2), .S(nfet_13_s));
  NFET nfet_14 (.G(RESET), .D(nfet_13_s), .S(R_t));

  // Other names for the same wires on the sheet: Q_t = Q_2

  // Notes on the sheet:
  //   R: default 1
endmodule
