// Digital circuit dffA.dig as structural Verilog
module dffA (
  input  D,
  input  C,
  input  R,
  input  S,
  output Q,
  output Q_2
);

  wire sr2x2_1_out_2, sr2x2_2_out, sr2x2_2_out_2;

  sr2x2 sr2x2_1 (.S__1(S), .S__2(sr2x2_2_out_2), .R__1(C), .R__2(R), .Out_2(sr2x2_1_out_2));  // open: Out
  sr2x2 sr2x2_2 (.S__1(sr2x2_1_out_2), .S__2(C), .R__1(D), .R__2(R), .Out(sr2x2_2_out), .Out_2(sr2x2_2_out_2));
  sr2x2 sr2x2_3 (.S__1(S), .S__2(sr2x2_1_out_2), .R__1(sr2x2_2_out), .R__2(R), .Out(Q), .Out_2(Q_2));

  // Notes on the sheet:
  //   R: default 1
  //   S: default 1
endmodule
