// Digital circuit dffR.dig as structural Verilog
module dffR (
  input  D,
  input  C,
  input  R,
  output Q,
  output Q_2
);

  wire sr1x2_1_out_2, sr2x2_1_out, sr2x2_1_out_2;

  sr1x2 sr1x2_1 (.S(sr2x2_1_out_2), .R__1(C), .R__2(R), .Out_2(sr1x2_1_out_2));  // open: Out
  sr2x2 sr2x2_1 (.S__1(sr1x2_1_out_2), .S__2(C), .R__1(D), .R__2(R), .Out(sr2x2_1_out), .Out_2(sr2x2_1_out_2));
  sr1x2 sr1x2_2 (.S(sr1x2_1_out_2), .R__1(sr2x2_1_out), .R__2(R), .Out(Q), .Out_2(Q_2));

  // Notes on the sheet:
  //   R: default 1
endmodule
