// Digital circuit dffRpd.dig as structural Verilog
module dffRpd (
  input  D,
  input  C,
  input  R,
  output Q,
  output Q_2
);

  wire sr2x1_1_out, sr2x1_1_out_2, sr_1_out_2;

  sr sr_1 (.S(sr2x1_1_out_2), .R(C), .Out_2(sr_1_out_2));  // open: Out
  sr2x1 sr2x1_1 (.S__1(sr_1_out_2), .S__2(C), .R(D), .Out(sr2x1_1_out), .Out_2(sr2x1_1_out_2));
  FGNFET fgnfet_1 (.G(R), .D(sr2x1_1_out), .S(1'b0));
  sr sr_2 (.S(sr_1_out_2), .R(sr2x1_1_out), .Out(Q), .Out_2(Q_2));
endmodule
