// Digital circuit tffA.dig as structural Verilog
module tffA (
  input  T,
  input  R,
  input  S,
  output Q,
  output Q_2
);

  dffAopt dffaopt_1 (.D(Q_2), .C(T), .Q(Q), .Q_2(Q_2), .R(R), .S(S));

  // Notes on the sheet:
  //   R: default 1
  //   S: default 1
endmodule
