// Digital circuit tffD.dig as structural Verilog
module tffD (
  input  T,
  input  E,
  input  D,
  output Q,
  output Q_2
);

  wire D_t, nfet_1_s, RESET, SET;

  \not  not_1 (.In(D), .Out(D_t));
  tffA tffa_1 (.T(T), .Q(Q), .Q_2(Q_2), .R(RESET), .S(SET));
  PullUp pullup_1 (.out(SET));
  NFET nfet_1 (.G(D), .D(SET), .S(nfet_1_s));
  NFET nfet_2 (.G(E), .D(nfet_1_s), .S(1'b0));
  PullUp pullup_2 (.out(RESET));
  NFET nfet_3 (.G(D_t), .D(RESET), .S(nfet_1_s));
endmodule
