// Digital circuit tffDR.dig as structural Verilog
module tffDR (
  input  T,
  input  E,
  input  D,
  input  R,
  output Q,
  output Q_2
);

  wire aoi2_1_1_out, D_t, nand_1_out;

  \not  not_1 (.In(D), .Out(D_t));
  tffA tffa_1 (.T(T), .Q(Q), .Q_2(Q_2), .R(aoi2_1_1_out), .S(nand_1_out));
  aoi2_1 aoi2_1_1 (.In_1A(D_t), .In_2A(E), .In_1B(R), .Out(aoi2_1_1_out));
  \nand  nand_1 (.In_1(E), .In_2(D), .Out(nand_1_out));
endmodule
