// Digital circuit tffR.dig as structural Verilog
module tffR (
  input  T,
  input  R,
  output Q,
  output Q_2
);

  dffRopt dffropt_1 (.D(Q_2), .C(T), .Q(Q), .Q_2(Q_2), .R(R));

  // Notes on the sheet:
  //   R: default 1
endmodule
