// Digital circuit nand4.dig as structural Verilog
module nand4 (
  input  In_1,
  input  In_2,
  input  In_3,
  input  In_4,
  output Out
);

  PullUp pullup_1 (.out(Out));
  s4 s4_1 (._1(In_1), ._2(In_2), ._3(In_3), ._4(In_4), .D(Out), .S(1'b0));

  // Other names for the same wires on the sheet: _1 = In_1; _2 = In_2; _3 = In_3; _4 = In_4
endmodule
