// Digital circuit nand5.dig as structural Verilog
module nand5 (
  input  In_1,
  input  In_2,
  input  In_3,
  input  In_4,
  input  In_5,
  output Out
);

  PullUp pullup_1 (.out(Out));
  s5 s5_1 (._1(In_1), ._2(In_2), ._3(In_3), ._4(In_4), ._5(In_5), .D(Out), .S(1'b0));

  // Other names for the same wires on the sheet: _1 = In_1; _2 = In_2; _3 = In_3; _4 = In_4; _5 = In_5
endmodule
