// Digital circuit nand7.dig as structural Verilog
module nand7 (
  input  In_1,
  input  In_2,
  input  In_3,
  input  In_4,
  input  In_5,
  input  In_6,
  input  In_7,
  output Out
);

  PullUp pullup_1 (.out(Out));
  s7 s7_1 (._1(In_1), ._2(In_2), ._3(In_3), ._4(In_4), ._5(In_5), ._6(In_6), ._7(In_7), .D(Out), .S(1'b0));

  // Other names for the same wires on the sheet: _1 = In_1; _2 = In_2; _3 = In_3; _4 = In_4; _5 = In_5; _6 = In_6;
  //   _7 = In_7
endmodule
