// Digital circuit aoi2-1.dig as structural Verilog
module aoi2_1 (
  input  In_1A,
  input  In_2A,
  input  In_1B,
  output Out
);

  PullUp pullup_1 (.out(Out));
  s2 s2_1 (._1(In_1A), ._2(In_2A), .D(Out), .S(1'b0));
  NFET nfet_1 (.G(In_1B), .D(Out), .S(1'b0));

  // Other names for the same wires on the sheet: _1A = In_1A; _1B = In_1B; _2A = In_2A
endmodule
