// Digital circuit nand.dig as structural Verilog
module \nand  (
  input  In_1,
  input  In_2,
  output Out
);

  PullUp pullup_1 (.out(Out));
  s2 s2_1 (._1(In_1), ._2(In_2), .D(Out), .S(1'b0));

  // Other names for the same wires on the sheet: _1 = In_1; _2 = In_2
endmodule
