// Digital circuit nand3.dig as structural Verilog
module nand3 (
  input  In_1,
  input  In_2,
  input  In_3,
  output Out
);

  PullUp pullup_1 (.out(Out));
  s3 s3_1 (._1(In_1), ._2(In_2), ._3(In_3), .D(Out), .S(1'b0));

  // Other names for the same wires on the sheet: _1 = In_1; _2 = In_2; _3 = In_3
endmodule
