// Digital circuit nandS2x1.dig as structural Verilog
module nandS2x1 (
  input  In_A1,
  input  In_B1,
  input  In_AB2,
  output Out_A,
  output Out_B
);

  wire nfet_1_d;

  p2D p2d_1 (._1(In_A1), ._2(In_B1), .D_1(Out_A), .D_2(Out_B), .S(nfet_1_d));
  NFET nfet_1 (.G(In_AB2), .D(nfet_1_d), .S(1'b0));
  PullUp pullup_1 (.out(Out_A));
  PullUp pullup_2 (.out(Out_B));

  // Other names for the same wires on the sheet: A1 = In_A1; AB2 = In_AB2; B1 = In_B1; OA = Out_A; OB = Out_B
endmodule
