// Digital circuit nand8x.dig as structural Verilog
module nand8x (
  input  [7:0] In_1,
  input  [7:0] In_2,
  output [7:0] Out
);

  nand4x nand4x_1 (.In_1(In_1[3:0]), .In_2(In_2[3:0]), .Out(Out[3:0]));
  nand4x nand4x_2 (.In_1(In_1[7:4]), .In_2(In_2[7:4]), .Out(Out[7:4]));

  // Other names for the same wires on the sheet: I1_0[3:0] = In_1[3:0]; I1_1[3:0] = In_1[7:4]; I2_0[3:0] = In_2[3:0];
  //   I2_1[3:0] = In_2[7:4]; O_0[3:0] = Out[3:0]; O_1[3:0] = Out[7:4]
endmodule
