// Digital circuit nor16x.dig as structural Verilog
module nor16x (
  input  [15:0] In_1,
  input  [15:0] In_2,
  output [15:0] Out
);

  nor8x nor8x_1 (.In_1(In_1[7:0]), .In_2(In_2[7:0]), .Out(Out[7:0]));
  nor8x nor8x_2 (.In_1(In_1[15:8]), .In_2(In_2[15:8]), .Out(Out[15:8]));

  // Other names for the same wires on the sheet: I1_0[7:0] = In_1[7:0]; I1_1[7:0] = In_1[15:8]; I2_0[7:0] = In_2[7:0];
  //   I2_1[7:0] = In_2[15:8]; O_0[7:0] = Out[7:0]; O_1[7:0] = Out[15:8]
endmodule
