// Digital circuit nor4x.dig as structural Verilog
module nor4x (
  input  [3:0] In_1,
  input  [3:0] In_2,
  output [3:0] Out
);

  \nor  nor_1 (.In_1(In_1[0]), .In_2(In_2[0]), .Out(Out[0]));
  \nor  nor_2 (.In_1(In_1[1]), .In_2(In_2[1]), .Out(Out[1]));
  \nor  nor_3 (.In_1(In_1[2]), .In_2(In_2[2]), .Out(Out[2]));
  \nor  nor_4 (.In_1(In_1[3]), .In_2(In_2[3]), .Out(Out[3]));

  // Other names for the same wires on the sheet: I1_0 = In_1[0]; I1_1 = In_1[1]; I1_2 = In_1[2]; I1_3 = In_1[3];
  //   I2_0 = In_2[0]; I2_1 = In_2[1]; I2_2 = In_2[2]; I2_3 = In_2[3]; O_0 = Out[0]; O_1 = Out[1]; O_2 = Out[2];
  //   O_3 = Out[3]
endmodule
