// Digital circuit not16x.dig as structural Verilog
module not16x (
  input  [15:0] In,
  output [15:0] Out
);

  not8x not8x_1 (.In(In[7:0]), .Out(Out[7:0]));
  not8x not8x_2 (.In(In[15:8]), .Out(Out[15:8]));

  // Other names for the same wires on the sheet: I_0[7:0] = In[7:0]; I_1[7:0] = In[15:8]; O_0[7:0] = Out[7:0];
  //   O_1[7:0] = Out[15:8]
endmodule
