// Digital circuit not4x.dig as structural Verilog
module not4x (
  input  [3:0] In,
  output [3:0] Out
);

  \not  not_1 (.In(In[0]), .Out(Out[0]));
  \not  not_2 (.In(In[1]), .Out(Out[1]));
  \not  not_3 (.In(In[2]), .Out(Out[2]));
  \not  not_4 (.In(In[3]), .Out(Out[3]));

  // Other names for the same wires on the sheet: I_0 = In[0]; I_1 = In[1]; I_2 = In[2]; I_3 = In[3]; O_0 = Out[0];
  //   O_1 = Out[1]; O_2 = Out[2]; O_3 = Out[3]
endmodule
