// Digital circuit not8x.dig as structural Verilog
module not8x (
  input  [7:0] In,
  output [7:0] Out
);

  not4x not4x_1 (.In(In[3:0]), .Out(Out[3:0]));
  not4x not4x_2 (.In(In[7:4]), .Out(Out[7:4]));

  // Other names for the same wires on the sheet: I_0[3:0] = In[3:0]; I_1[3:0] = In[7:4]; O_0[3:0] = Out[3:0];
  //   O_1[3:0] = Out[7:4]
endmodule
