// Digital circuit and4D.dig as structural Verilog
module and4D (
  input  In_1,
  input  In_2,
  input  In_3,
  input  In_4,
  output Out,
  output Out_2
);

  nand4 nand4_1 (.In_1(In_1), .In_2(In_2), .In_3(In_3), .In_4(In_4), .Out(Out_2));
  \not  not_1 (.In(Out_2), .Out(Out));

  // Other names for the same wires on the sheet: _1 = In_1; _2 = In_2; _3 = In_3; _4 = In_4
endmodule
