// Digital circuit and8D.dig as structural Verilog
module and8D (
  input  In_1,
  input  In_2,
  input  In_3,
  input  In_4,
  input  In_5,
  input  In_6,
  input  In_7,
  input  In_8,
  output Out,
  output Out_2
);

  nand8 nand8_1 (
    .In_1(In_1), .In_2(In_2), .In_3(In_3), .In_4(In_4), .In_5(In_5), .In_6(In_6), .In_7(In_7), .In_8(In_8),
    .Out(Out_2));
  \not  not_1 (.In(Out_2), .Out(Out));

  // Other names for the same wires on the sheet: _1 = In_1; _2 = In_2; _3 = In_3; _4 = In_4; _5 = In_5; _6 = In_6;
  //   _7 = In_7; _8 = In_8
endmodule
