// Digital circuit and.dig as structural Verilog
module \and  (
  input  In_1,
  input  In_2,
  output Out
);

  wire nand_1_out;

  \nand  nand_1 (.In_1(In_1), .In_2(In_2), .Out(nand_1_out));
  \not  not_1 (.In(nand_1_out), .Out(Out));

  // Other names for the same wires on the sheet: _1 = In_1; _2 = In_2
endmodule
