// Digital circuit and11.dig as structural Verilog
module and11 (
  input  In_1,
  input  In_2,
  input  In_3,
  input  In_4,
  input  In_5,
  input  In_6,
  input  In_7,
  input  In_8,
  input  In_9,
  input  In_10,
  input  In_11,
  output Out
);

  wire nand11_1_out;

  nand11 nand11_1 (
    .In_1(In_1), .In_2(In_2), .In_3(In_3), .In_4(In_4), .In_5(In_5), .In_6(In_6), .In_7(In_7), .In_8(In_8),
    .In_9(In_9), .In_10(In_10), .In_11(In_11), .Out(nand11_1_out));
  \not  not_1 (.In(nand11_1_out), .Out(Out));

  // Other names for the same wires on the sheet: _1 = In_1; _2 = In_2; _3 = In_3; _4 = In_4; _5 = In_5; _6 = In_6;
  //   _7 = In_7; _8 = In_8; _9 = In_9; _10 = In_10; _11 = In_11
endmodule
