// Digital circuit and3.dig as structural Verilog
module and3 (
  input  In_1,
  input  In_2,
  input  In_3,
  output Out
);

  wire nand3_1_out;

  nand3 nand3_1 (.In_1(In_1), .In_2(In_2), .In_3(In_3), .Out(nand3_1_out));
  \not  not_1 (.In(nand3_1_out), .Out(Out));

  // Other names for the same wires on the sheet: _1 = In_1; _2 = In_2; _3 = In_3
endmodule
