// Digital circuit and4.dig as structural Verilog
module and4 (
  input  In_1,
  input  In_2,
  input  In_3,
  input  In_4,
  output Out
);

  wire nand4_1_out;

  nand4 nand4_1 (.In_1(In_1), .In_2(In_2), .In_3(In_3), .In_4(In_4), .Out(nand4_1_out));
  \not  not_1 (.In(nand4_1_out), .Out(Out));

  // Other names for the same wires on the sheet: _1 = In_1; _2 = In_2; _3 = In_3; _4 = In_4
endmodule
