// Digital circuit and5.dig as structural Verilog
module and5 (
  input  In_1,
  input  In_2,
  input  In_3,
  input  In_4,
  input  In_5,
  output Out
);

  wire nand5_1_out;

  nand5 nand5_1 (.In_1(In_1), .In_2(In_2), .In_3(In_3), .In_4(In_4), .In_5(In_5), .Out(nand5_1_out));
  \not  not_1 (.In(nand5_1_out), .Out(Out));

  // Other names for the same wires on the sheet: _1 = In_1; _2 = In_2; _3 = In_3; _4 = In_4; _5 = In_5
endmodule
