// Digital circuit and6.dig as structural Verilog
module and6 (
  input  In_1,
  input  In_2,
  input  In_3,
  input  In_4,
  input  In_5,
  input  In_6,
  output Out
);

  wire nand6_1_out;

  nand6 nand6_1 (.In_1(In_1), .In_2(In_2), .In_3(In_3), .In_4(In_4), .In_5(In_5), .In_6(In_6), .Out(nand6_1_out));
  \not  not_1 (.In(nand6_1_out), .Out(Out));

  // Other names for the same wires on the sheet: _1 = In_1; _2 = In_2; _3 = In_3; _4 = In_4; _5 = In_5; _6 = In_6
endmodule
