// Digital circuit orD.dig as structural Verilog
module orD (
  input  In_1,
  input  In_2,
  output Out,
  output Out_2
);

  \nor  nor_1 (.In_1(In_1), .In_2(In_2), .Out(Out_2));
  \not  not_1 (.In(Out_2), .Out(Out));

  // Other names for the same wires on the sheet: _1 = In_1; _2 = In_2
endmodule
