// Digital circuit or.dig as structural Verilog
module \or  (
  input  In_1,
  input  In_2,
  output Out
);

  wire nor_1_out;

  \nor  nor_1 (.In_1(In_1), .In_2(In_2), .Out(nor_1_out));
  \not  not_1 (.In(nor_1_out), .Out(Out));

  // Other names for the same wires on the sheet: _1 = In_1; _2 = In_2
endmodule
