// Digital circuit rs.dig as structural Verilog
module rs (
  input  S,
  input  R,
  output Out,
  output Out_2
);

  \nor  nor_1 (.In_1(R), .In_2(Out_2), .Out(Out));
  \nor  nor_2 (.In_1(Out), .In_2(S), .Out(Out_2));
endmodule
