// Digital circuit rs2x1.dig as structural Verilog
module rs2x1 (
  input  S,
  input  R_2,
  input  R_1,
  output Out,
  output Out_2
);

  nor3 nor3_1 (.In_1(R_1), .In_2(R_2), .In_3(Out_2), .Out(Out));
  \nor  nor_1 (.In_1(Out), .In_2(S), .Out(Out_2));

  // Other names for the same wires on the sheet: R1 = R_1; R2 = R_2
endmodule
