// Digital circuit rs2x2.dig as structural Verilog
module rs2x2 (
  input  S_1,
  input  R_2,
  input  R_1,
  input  S_2,
  output Out,
  output Out_2
);

  nor3 nor3_1 (.In_1(R_1), .In_2(R_2), .In_3(Out_2), .Out(Out));
  nor3 nor3_2 (.In_1(Out), .In_2(S_1), .In_3(S_2), .Out(Out_2));

  // Other names for the same wires on the sheet: R1 = R_1; R2 = R_2; S1 = S_1; S2 = S_2
endmodule
