// Digital circuit sr.dig as structural Verilog
module sr (
  input  S,
  input  R,
  output Out,
  output Out_2
);

  \nand  nand_1 (.In_1(S), .In_2(Out_2), .Out(Out));
  \nand  nand_2 (.In_1(Out), .In_2(R), .Out(Out_2));

  // Notes on the sheet:
  //   S: default 1
  //   R: default 1
endmodule
