// Digital circuit sr1x2.dig as structural Verilog
module sr1x2 (
  input  S,
  input  R__2,
  input  R__1,
  output Out,
  output Out_2
);

  \nand  nand_1 (.In_1(S), .In_2(Out_2), .Out(Out));
  nand3 nand3_1 (.In_1(Out), .In_2(R__1), .In_3(R__2), .Out(Out_2));

  // Other names for the same wires on the sheet: R1 = R__1; R2 = R__2

  // Notes on the sheet:
  //   S: default 1
  //   R__2: default 1
  //   R__1: default 1
endmodule
