// Digital circuit sr2x1.dig as structural Verilog
module sr2x1 (
  input  S__1,
  input  R,
  input  S__2,
  output Out,
  output Out_2
);

  nand3 nand3_1 (.In_1(S__1), .In_2(S__2), .In_3(Out_2), .Out(Out));
  \nand  nand_1 (.In_1(Out), .In_2(R), .Out(Out_2));

  // Other names for the same wires on the sheet: S1 = S__1; S2 = S__2

  // Notes on the sheet:
  //   S__1: default 1
  //   R: default 1
  //   S__2: default 1
endmodule
