// Digital circuit sr2x2.dig as structural Verilog
module sr2x2 (
  input  S__1,
  input  R__2,
  input  R__1,
  input  S__2,
  output Out,
  output Out_2
);

  nand3 nand3_1 (.In_1(S__1), .In_2(S__2), .In_3(Out_2), .Out(Out));
  nand3 nand3_2 (.In_1(Out), .In_2(R__1), .In_3(R__2), .Out(Out_2));

  // Other names for the same wires on the sheet: R1 = R__1; R2 = R__2; S1 = S__1; S2 = S__2

  // Notes on the sheet:
  //   S__1: default 1
  //   R__2: default 1
  //   R__1: default 1
  //   S__2: default 1
endmodule
