// Digital circuit sr_min.dig as structural Verilog
module sr_min (
  input  S,
  input  R,
  output Q,
  output Q_2
);

  NFET nfet_1 (.G(S), .D(R), .S(1'b0));
  NFET nfet_2 (.G(R), .D(S), .S(1'b0));

  assign Q = S;
  assign Q_2 = R;

  // Other names for the same wires on the sheet: Q_t = R
endmodule
