// Digital circuit sr_real.dig as structural Verilog
module sr_real (
  input  S,
  input  R,
  output Q,
  output Q_2
);

  PullUp pullup_1 (.out(R));
  NFET nfet_1 (.G(S), .D(R), .S(1'b0));
  PullUp pullup_2 (.out(S));
  NFET nfet_2 (.G(R), .D(S), .S(1'b0));

  assign Q = S;
  assign Q_2 = R;

  // Other names for the same wires on the sheet: Q_t = R
endmodule
