// Digital circuit d.dig as structural Verilog
module d (
  input  D,
  input  E,
  output Q,
  output Q_2
);

  wire D_t;

  s2 s2_1 (._1(E), ._2(D), .D(Q_2), .S(1'b0));
  \not  not_1 (.In(D), .Out(D_t));
  s2 s2_2 (._1(E), ._2(D_t), .D(Q), .S(1'b0));
  sr_real sr_real_1 (.S(Q), .R(Q_2), .Q(Q), .Q_2(Q_2));

  // Other names for the same wires on the sheet: Q_t = Q_2
endmodule
