// Digital circuit counter16S.dig as structural Verilog
module counter16S (
  input  C,
  input  [15:0] D,
  input  S,
  output [15:0] Out,
  output [15:0] Out_2
);

  counter8S counter8s_1 (.C(C), .D(D[7:0]), .S(S), .Out(Out[7:0]), .Out_2(Out_2[7:0]));
  counter8S counter8s_2 (.C(Out_2[7]), .D(D[15:8]), .S(S), .Out(Out[15:8]), .Out_2(Out_2[15:8]));

  // Other names for the same wires on the sheet: _0[7:0] = Out[7:0]; _0_t[7:0] = Out_2[7:0]; _1[7:0] = Out[15:8];
  //   _1_t[7:0] = Out_2[15:8]; D_0[7:0] = D[7:0]; D_1[7:0] = D[15:8]
endmodule
