// Digital circuit counter2S.dig as structural Verilog
module counter2S (
  input  C,
  input  [1:0] D,
  input  S,
  output [1:0] Out,
  output [1:0] Out_2
);

  tffD tffd_1 (.T(C), .D(D[0]), .E(S), .Q(Out[0]), .Q_2(Out_2[0]));
  tffD tffd_2 (.T(Out_2[0]), .D(D[1]), .E(S), .Q(Out[1]), .Q_2(Out_2[1]));

  // Other names for the same wires on the sheet: _0 = Out[0]; _0_t = Out_2[0]; _1 = Out[1]; _1_t = Out_2[1];
  //   D_0 = D[0]; D_1 = D[1]
endmodule
