// Digital circuit counter3SR.dig as structural Verilog
module counter3SR (
  input  C,
  input  [2:0] D,
  input  S,
  input  R,
  output [2:0] Out,
  output [2:0] Out_2
);

  counter2SR counter2sr_1 (.C(C), .D(D[1:0]), .S(S), .Out(Out[1:0]), .Out_2(Out_2[1:0]), .R(R));
  tffDR tffdr_1 (.T(Out_2[1]), .D(D[2]), .E(S), .Q(Out[2]), .Q_2(Out_2[2]), .R(R));

  // Other names for the same wires on the sheet: _0[1:0] = Out[1:0]; _0_t[1:0] = Out_2[1:0]; _1 = Out[2];
  //   _1_t = Out_2[2]; D_0[1:0] = D[1:0]; D_1 = D[2]
endmodule
