// Digital circuit counter4S.dig as structural Verilog
module counter4S (
  input  C,
  input  [3:0] D,
  input  S,
  output [3:0] Out,
  output [3:0] Out_2
);

  counter2S counter2s_1 (.C(C), .D(D[1:0]), .S(S), .Out(Out[1:0]), .Out_2(Out_2[1:0]));
  counter2S counter2s_2 (.C(Out_2[1]), .D(D[3:2]), .S(S), .Out(Out[3:2]), .Out_2(Out_2[3:2]));

  // Other names for the same wires on the sheet: _0[1:0] = Out[1:0]; _0_t[1:0] = Out_2[1:0]; _1[1:0] = Out[3:2];
  //   _1_t[1:0] = Out_2[3:2]; D_0[1:0] = D[1:0]; D_1[1:0] = D[3:2]
endmodule
