// Digital circuit counter6SR.dig as structural Verilog
module counter6SR (
  input  C,
  input  [5:0] D,
  input  S,
  input  R,
  output [5:0] Out,
  output [5:0] Out_2
);

  counter4SR counter4sr_1 (.C(C), .D(D[3:0]), .S(S), .Out(Out[3:0]), .Out_2(Out_2[3:0]), .R(R));
  counter2SR counter2sr_1 (.C(Out_2[3]), .D(D[5:4]), .S(S), .Out(Out[5:4]), .Out_2(Out_2[5:4]), .R(R));

  // Other names for the same wires on the sheet: _0[3:0] = Out[3:0]; _0_t[3:0] = Out_2[3:0]; _1[1:0] = Out[5:4];
  //   _1_t[1:0] = Out_2[5:4]; D_0[3:0] = D[3:0]; D_1[1:0] = D[5:4]
endmodule
