// Digital circuit counter8S.dig as structural Verilog
module counter8S (
  input  C,
  input  [7:0] D,
  input  S,
  output [7:0] Out,
  output [7:0] Out_2
);

  counter4S counter4s_1 (.C(C), .D(D[3:0]), .S(S), .Out(Out[3:0]), .Out_2(Out_2[3:0]));
  counter4S counter4s_2 (.C(Out_2[3]), .D(D[7:4]), .S(S), .Out(Out[7:4]), .Out_2(Out_2[7:4]));

  // Other names for the same wires on the sheet: _0[3:0] = Out[3:0]; _0_t[3:0] = Out_2[3:0]; _1[3:0] = Out[7:4];
  //   _1_t[3:0] = Out_2[7:4]; D_0[3:0] = D[3:0]; D_1[3:0] = D[7:4]
endmodule
