// Digital circuit counter16.dig as structural Verilog
module counter16 (
  input  C,
  input  R,
  output [15:0] Out,
  output [15:0] Out_2
);

  counter8 counter8_1 (.C(C), .Out(Out[7:0]), .Out_2(Out_2[7:0]), .R(R));
  counter8 counter8_2 (.C(Out_2[7]), .Out(Out[15:8]), .Out_2(Out_2[15:8]), .R(R));

  // Other names for the same wires on the sheet: _0[7:0] = Out[7:0]; _0_t[7:0] = Out_2[7:0]; _1[7:0] = Out[15:8];
  //   _1_t[7:0] = Out_2[15:8]
endmodule
