// Digital circuit counter2.dig as structural Verilog
module counter2 (
  input  C,
  input  R,
  output [1:0] Out,
  output [1:0] Out_2
);

  tffR tffr_1 (.T(C), .Q(Out[0]), .Q_2(Out_2[0]), .R(R));
  tffR tffr_2 (.T(Out_2[0]), .Q(Out[1]), .Q_2(Out_2[1]), .R(R));

  // Other names for the same wires on the sheet: _0 = Out[0]; _0_t = Out_2[0]; _1 = Out[1]; _1_t = Out_2[1]

  // Notes on the sheet:
  //   R: default 1
endmodule
