// Digital circuit counter3.dig as structural Verilog
module counter3 (
  input  C,
  input  R,
  output [2:0] Out,
  output [2:0] Out_2
);

  counter2 counter2_1 (.C(C), .Out(Out[1:0]), .Out_2(Out_2[1:0]), .R(R));
  tffR tffr_1 (.T(Out_2[1]), .Q(Out[2]), .Q_2(Out_2[2]), .R(R));

  // Other names for the same wires on the sheet: _0[1:0] = Out[1:0]; _0_t[1:0] = Out_2[1:0]; _1 = Out[2];
  //   _1_t = Out_2[2]

  // Notes on the sheet:
  //   R: default 1
endmodule
