// Digital circuit counter4.dig as structural Verilog
module counter4 (
  input  C,
  input  R,
  output [3:0] Out,
  output [3:0] Out_2
);

  tffR tffr_1 (.T(C), .Q(Out[0]), .Q_2(Out_2[0]), .R(R));
  tffR tffr_2 (.T(Out_2[0]), .Q(Out[1]), .Q_2(Out_2[1]), .R(R));
  tffR tffr_3 (.T(Out_2[1]), .Q(Out[2]), .Q_2(Out_2[2]), .R(R));
  tffR tffr_4 (.T(Out_2[2]), .Q(Out[3]), .Q_2(Out_2[3]), .R(R));

  // Other names for the same wires on the sheet: _0 = Out[0]; _0_t = Out_2[0]; _1 = Out[1]; _1_t = Out_2[1];
  //   _2 = Out[2]; _2_t = Out_2[2]; _3 = Out[3]; _3_t = Out_2[3]
endmodule
