// Digital circuit counter6.dig as structural Verilog
module counter6 (
  input  C,
  input  R,
  output [5:0] Out,
  output [5:0] Out_2
);

  counter4 counter4_1 (.C(C), .Out(Out[3:0]), .Out_2(Out_2[3:0]), .R(R));
  counter2 counter2_1 (.C(Out_2[3]), .Out(Out[5:4]), .Out_2(Out_2[5:4]), .R(R));

  // Other names for the same wires on the sheet: _0[3:0] = Out[3:0]; _0_t[3:0] = Out_2[3:0]; _1[1:0] = Out[5:4];
  //   _1_t[1:0] = Out_2[5:4]

  // Notes on the sheet:
  //   R: default 1
endmodule
