// Digital circuit counter8.dig as structural Verilog
module counter8 (
  input  C,
  input  R,
  output [7:0] Out,
  output [7:0] Out_2
);

  counter4 counter4_1 (.C(C), .Out(Out[3:0]), .Out_2(Out_2[3:0]), .R(R));
  counter4 counter4_2 (.C(Out_2[3]), .Out(Out[7:4]), .Out_2(Out_2[7:4]), .R(R));

  // Other names for the same wires on the sheet: _0[3:0] = Out[3:0]; _0_t[3:0] = Out_2[3:0]; _1[3:0] = Out[7:4];
  //   _1_t[3:0] = Out_2[7:4]
endmodule
