// Digital circuit p2D.dig as structural Verilog
module p2D (
  input  _1,
  input  _2,
  input  D_1,
  input  S,
  input  D_2
);

  NFET nfet_1 (.G(_1), .D(D_1), .S(S));
  NFET nfet_2 (.G(_2), .D(D_2), .S(S));
endmodule
