// Digital circuit p2S.dig as structural Verilog
module p2S (
  input  _1,
  input  _2,
  input  D_1,
  input  S_1,
  input  S_2
);

  NFET nfet_1 (.G(_1), .D(D_1), .S(S_1));
  NFET nfet_2 (.G(_2), .D(D_1), .S(S_2));
endmodule
