// Digital circuit p16.dig as structural Verilog
module p16 (
  input  _1,
  input  _2,
  input  D,
  input  S,
  input  _3,
  input  _4,
  input  _5,
  input  _6,
  input  _7,
  input  _8,
  input  _9,
  input  _10,
  input  _11,
  input  _12,
  input  _13,
  input  _14,
  input  _15,
  input  _16
);

  NFET nfet_1 (.G(_1), .D(D), .S(S));
  NFET nfet_2 (.G(_2), .D(D), .S(S));
  NFET nfet_3 (.G(_3), .D(D), .S(S));
  NFET nfet_4 (.G(_4), .D(D), .S(S));
  NFET nfet_5 (.G(_5), .D(D), .S(S));
  NFET nfet_6 (.G(_6), .D(D), .S(S));
  NFET nfet_7 (.G(_7), .D(D), .S(S));
  NFET nfet_8 (.G(_8), .D(D), .S(S));
  NFET nfet_9 (.G(_9), .D(D), .S(S));
  NFET nfet_10 (.G(_10), .D(D), .S(S));
  NFET nfet_11 (.G(_11), .D(D), .S(S));
  NFET nfet_12 (.G(_12), .D(D), .S(S));
  NFET nfet_13 (.G(_13), .D(D), .S(S));
  NFET nfet_14 (.G(_14), .D(D), .S(S));
  NFET nfet_15 (.G(_15), .D(D), .S(S));
  NFET nfet_16 (.G(_16), .D(D), .S(S));
endmodule
