// Digital circuit p3.dig as structural Verilog
module p3 (
  input  _1,
  input  _2,
  input  D,
  input  S,
  input  _3
);

  NFET nfet_1 (.G(_1), .D(D), .S(S));
  NFET nfet_2 (.G(_2), .D(D), .S(S));
  NFET nfet_3 (.G(_3), .D(D), .S(S));
endmodule
