// Digital circuit p7.dig as structural Verilog
module p7 (
  input  _1,
  input  _2,
  input  D,
  input  S,
  input  _3,
  input  _4,
  input  _5,
  input  _6,
  input  _7
);

  NFET nfet_1 (.G(_1), .D(D), .S(S));
  NFET nfet_2 (.G(_2), .D(D), .S(S));
  NFET nfet_3 (.G(_3), .D(D), .S(S));
  NFET nfet_4 (.G(_4), .D(D), .S(S));
  NFET nfet_5 (.G(_5), .D(D), .S(S));
  NFET nfet_6 (.G(_6), .D(D), .S(S));
  NFET nfet_7 (.G(_7), .D(D), .S(S));
endmodule
