// Digital circuit s16.dig as structural Verilog
module s16 (
  input  _1,
  input  _2,
  input  D,
  input  S,
  input  _3,
  input  _4,
  input  _5,
  input  _6,
  input  _7,
  input  _8,
  input  _9,
  input  _10,
  input  _11,
  input  _12,
  input  _13,
  input  _14,
  input  _15,
  input  _16
);

  wire nfet_1_s, nfet_2_s, nfet_3_s, nfet_4_s, nfet_5_s, nfet_6_s, nfet_7_s, nfet_8_s, nfet_9_s, nfet_10_s,
       nfet_11_s, nfet_12_s, nfet_13_s, nfet_14_s, nfet_15_s;

  NFET nfet_1 (.G(_1), .D(D), .S(nfet_1_s));
  NFET nfet_2 (.G(_2), .D(nfet_1_s), .S(nfet_2_s));
  NFET nfet_3 (.G(_3), .D(nfet_2_s), .S(nfet_3_s));
  NFET nfet_4 (.G(_4), .D(nfet_3_s), .S(nfet_4_s));
  NFET nfet_5 (.G(_5), .D(nfet_4_s), .S(nfet_5_s));
  NFET nfet_6 (.G(_6), .D(nfet_5_s), .S(nfet_6_s));
  NFET nfet_7 (.G(_7), .D(nfet_6_s), .S(nfet_7_s));
  NFET nfet_8 (.G(_8), .D(nfet_7_s), .S(nfet_8_s));
  NFET nfet_9 (.G(_9), .D(nfet_8_s), .S(nfet_9_s));
  NFET nfet_10 (.G(_10), .D(nfet_9_s), .S(nfet_10_s));
  NFET nfet_11 (.G(_11), .D(nfet_10_s), .S(nfet_11_s));
  NFET nfet_12 (.G(_12), .D(nfet_11_s), .S(nfet_12_s));
  NFET nfet_13 (.G(_13), .D(nfet_12_s), .S(nfet_13_s));
  NFET nfet_14 (.G(_14), .D(nfet_13_s), .S(nfet_14_s));
  NFET nfet_15 (.G(_15), .D(nfet_14_s), .S(nfet_15_s));
  NFET nfet_16 (.G(_16), .D(nfet_15_s), .S(S));
endmodule
