// Digital circuit s3.dig as structural Verilog
module s3 (
  input  _1,
  input  _2,
  input  D,
  input  S,
  input  _3
);

  wire nfet_1_s, nfet_2_s;

  NFET nfet_1 (.G(_1), .D(D), .S(nfet_1_s));
  NFET nfet_2 (.G(_2), .D(nfet_1_s), .S(nfet_2_s));
  NFET nfet_3 (.G(_3), .D(nfet_2_s), .S(S));
endmodule
