// Digital circuit s4.dig as structural Verilog
module s4 (
  input  _1,
  input  _2,
  input  D,
  input  S,
  input  _3,
  input  _4
);

  wire nfet_1_s, nfet_2_s, nfet_3_s;

  NFET nfet_1 (.G(_1), .D(D), .S(nfet_1_s));
  NFET nfet_2 (.G(_2), .D(nfet_1_s), .S(nfet_2_s));
  NFET nfet_3 (.G(_3), .D(nfet_2_s), .S(nfet_3_s));
  NFET nfet_4 (.G(_4), .D(nfet_3_s), .S(S));
endmodule
