// Digital circuit binary_clock_hms_bcd.dig as structural Verilog
module binary_clock_hms_bcd (
  input  clk,
  output [3:0] S0,
  output [2:0] S1,
  output [3:0] M0,
  output [2:0] M1
);

  wire M0_0_t, M0_1_t, M0_2_t, M0_3_t, M0_R, M0_R_t, M1_0_t, M1_1_t, M1_2_t, M1_R, M1_R_t, nor_1_out,
       nor_2_out, S0_0_t, S0_1_t, S0_2_t, S0_3_t, S0_R, S0_R_t, S1_0_t, S1_1_t, S1_2_t, S1_R, S1_R_t, Set;
  wire [1:0] D_H1;
  wire [2:0] D_M1;
  wire [3:0] D_H0, D_M0;

  DipSwitch dipswitch_1 (.out(D_H1[1]));
  counter4 counter4_1 (.Out(S0), .Out_2({S0_3_t, S0_2_t, S0_1_t, S0_0_t}), .C(clk), .R(nor_1_out));
  \nor  nor_1 (.In_1(Set), .In_2(S0_R), .Out(nor_1_out));
  \nand  nand_1 (.In_1(S0[1]), .In_2(S0[3]), .Out(S0_R_t));
  \not  not_1 (.In(S0_R_t), .Out(S0_R));
  DipSwitch dipswitch_2 (.out(D_H0[2]));
  DipSwitch dipswitch_3 (.out(D_H0[3]));
  DipSwitch dipswitch_4 (.out(D_H1[0]));
  DipSwitch dipswitch_5 (.out(D_H0[0]));
  DipSwitch dipswitch_6 (.out(D_H0[1]));
  DipSwitch dipswitch_7 (.out(D_M1[0]));
  DipSwitch dipswitch_8 (.out(D_M1[1]));
  DipSwitch dipswitch_9 (.out(D_M1[2]));
  DipSwitch dipswitch_10 (.out(D_M0[0]));
  DipSwitch dipswitch_11 (.out(D_M0[1]));
  DipSwitch dipswitch_12 (.out(D_M0[2]));
  DipSwitch dipswitch_13 (.out(D_M0[3]));
  counter3 counter3_1 (.Out(S1), .Out_2({S1_2_t, S1_1_t, S1_0_t}), .C(S0_R), .R(nor_2_out));
  \nor  nor_2 (.In_1(Set), .In_2(S1_R), .Out(nor_2_out));
  \nand  nand_2 (.In_1(S1[1]), .In_2(S1[2]), .Out(S1_R_t));
  \not  not_2 (.In(S1_R_t), .Out(S1_R));
  Button button_1 (.out(Set));
  LED led_1 ();  // open: in
  LED led_2 ();  // open: in
  counter4SR counter4sr_1 (.C(S1_R), .D(D_M0), .S(Set), .Out(M0), .Out_2({M0_3_t, M0_2_t, M0_1_t, M0_0_t}), .R(M0_R));
  \nand  nand_3 (.In_1(M0[1]), .In_2(M0[3]), .Out(M0_R_t));
  \not  not_3 (.In(M0_R_t), .Out(M0_R));
  LED led_3 ();  // open: in
  LED led_4 ();  // open: in
  LED led_5 ();  // open: in
  LED led_6 ();  // open: in
  LED led_7 (.in(M1[2]));
  LED led_8 (.in(M1[1]));
  LED led_9 (.in(M1[0]));
  LED led_10 (.in(M0[3]));
  LED led_11 (.in(M0[2]));
  LED led_12 (.in(M0[1]));
  LED led_13 (.in(M0[0]));
  counter3SR counter3sr_1 (.C(M0_R), .D(D_M1), .S(Set), .Out(M1), .Out_2({M1_2_t, M1_1_t, M1_0_t}), .R(M1_R));
  \nand  nand_4 (.In_1(M1[1]), .In_2(M1[2]), .Out(M1_R_t));
  \not  not_4 (.In(M1_R_t), .Out(M1_R));
  LED led_14 (.in(S1[2]));
  LED led_15 (.in(S1[1]));
  LED led_16 (.in(S1[0]));
  LED led_17 (.in(S0[3]));
  LED led_18 (.in(S0[2]));
  LED led_19 (.in(S0[1]));
  LED led_20 (.in(S0[0]));

  // Other names for the same wires on the sheet: M0_0 = M0[0]; M0_1 = M0[1]; M0_2 = M0[2]; M0_3 = M0[3]; M1_0 = M1[0];
  //   M1_1 = M1[1]; M1_2 = M1[2]; S0_0 = S0[0]; S0_1 = S0[1]; S0_2 = S0[2]; S0_3 = S0[3]; S1_0 = S1[0]; S1_1 = S1[1];
  //   S1_2 = S1[2]

  // Notes on the sheet:
  //   Hours
  //   Minutes
  //   Set
  //   Seconds
  //   8
  //   4
  //   2
  //   1
endmodule
