// Digital circuit binary_clock_hms_sex.dig as structural Verilog
module binary_clock_hms_sex (
  input  clk,
  output [5:0] S,
  output [5:0] M,
  output [3:0] H,
  output PM,
  output AM
);

  wire Clk_t, D_PM, H_0_t, H_1_t, H_2_t, H_3_t, H_R, M_0_t, M_1_t, M_2_t, M_3_t, M_4_t, M_5_t, M_R,
       nor_1_out, S_0_t, S_1_t, S_2_t, S_3_t, S_4_t, S_5_t, S_R, Set;
  wire [3:0] D_H;
  wire [5:0] D_M;

  tff tff_1 (.T(clk), .Q(Clk_t));  // open: Q_2
  counter6 counter6_1 (.C(Clk_t), .Out(S), .Out_2({S_5_t, S_4_t, S_3_t, S_2_t, S_1_t, S_0_t}), .R(nor_1_out));
  \nor  nor_1 (.In_1(Set), .In_2(S_R), .Out(nor_1_out));
  counter6SR counter6sr_1 (
    .C(S_R), .D(D_M), .S(Set), .Out(M), .Out_2({M_5_t, M_4_t, M_3_t, M_2_t, M_1_t, M_0_t}), .R(M_R));
  nor4 nor4_1 (.In_1(S_2_t), .In_2(S_3_t), .In_3(S_4_t), .In_4(S_5_t), .Out(S_R));
  DipSwitch dipswitch_1 (.out(D_PM));
  DipSwitch dipswitch_2 (.out(D_H[0]));
  DipSwitch dipswitch_3 (.out(D_H[1]));
  DipSwitch dipswitch_4 (.out(D_H[2]));
  DipSwitch dipswitch_5 (.out(D_H[3]));
  DipSwitch dipswitch_6 (.out(D_M[4]));
  DipSwitch dipswitch_7 (.out(D_M[5]));
  counter4SR counter4sr_1 (.C(M_R), .D(D_H), .S(Set), .Out(H), .Out_2({H_3_t, H_2_t, H_1_t, H_0_t}), .R(H_R));
  nor4 nor4_2 (.In_1(M_2_t), .In_2(M_3_t), .In_3(M_4_t), .In_4(M_5_t), .Out(M_R));
  DipSwitch dipswitch_8 (.out(D_M[0]));
  DipSwitch dipswitch_9 (.out(D_M[1]));
  DipSwitch dipswitch_10 (.out(D_M[2]));
  DipSwitch dipswitch_11 (.out(D_M[3]));
  Button button_1 (.out(Set));
  tffD tffd_1 (.T(H_R), .D(D_PM), .E(Set), .Q(PM), .Q_2(AM));
  \nor  nor_2 (.In_1(H_2_t), .In_2(H_3_t), .Out(H_R));
  LED led_1 (.in(PM));
  LED led_2 (.in(AM));
  // RGBLED rgbled_1: pin names not known; wires that end beside it: AM, PM
  // RGBLED rgbled_2: pin names not known; wires that end beside it: AM, PM
  // RGBLED rgbled_3: pin names not known; wires that end beside it: AM, PM
  // RGBLED rgbled_4: pin names not known; wires that end beside it: AM, PM
  // RGBLED rgbled_5: pin names not known; wires that end beside it: AM, PM
  // RGBLED rgbled_6: pin names not known; wires that end beside it: AM, PM
  // RGBLED rgbled_7: pin names not known; wires that end beside it: PM, AM
  // RGBLED rgbled_8: pin names not known; wires that end beside it: PM, AM
  LED led_3 (.in(H[3]));
  LED led_4 (.in(M[5]));
  LED led_5 (.in(M[4]));
  LED led_6 (.in(S[5]));
  LED led_7 (.in(S[4]));
  // RGBLED rgbled_9: pin names not known; wires that end beside it: AM, PM
  // RGBLED rgbled_10: pin names not known; wires that end beside it: AM, PM
  // RGBLED rgbled_11: pin names not known; wires that end beside it: PM, AM
  LED led_8 (.in(H[2]));
  LED led_9 (.in(H[1]));
  LED led_10 (.in(M[3]));
  LED led_11 (.in(M[2]));
  LED led_12 (.in(S[3]));
  LED led_13 (.in(S[2]));
  // RGBLED rgbled_12: pin names not known; wires that end beside it: AM, PM
  // RGBLED rgbled_13: pin names not known; wires that end beside it: PM, AM
  LED led_14 (.in(H[0]));
  LED led_15 (.in(M[1]));
  LED led_16 (.in(M[0]));
  LED led_17 (.in(S[1]));
  LED led_18 (.in(S[0]));
  // RGBLED rgbled_14: pin names not known; wires that end beside it: AM, PM
  // RGBLED rgbled_15: pin names not known; wires that end beside it: PM, AM
  // RGBLED rgbled_16: pin names not known; wires that end beside it: PM, AM
  // RGBLED rgbled_17: pin names not known; wires that end beside it: PM, AM
  // RGBLED rgbled_18: pin names not known; wires that end beside it: PM, AM
  // RGBLED rgbled_19: pin names not known; wires that end beside it: PM, AM
  // RGBLED rgbled_20: pin names not known; wires that end beside it: PM, AM
  // RGBLED rgbled_21: pin names not known; wires that end beside it: PM, AM
  // RGBLED rgbled_22: pin names not known; wires that end beside it: AM, PM

  // Other names for the same wires on the sheet: H_0 = H[0]; H_1 = H[1]; H_2 = H[2]; H_3 = H[3]; M_0 = M[0];
  //   M_1 = M[1]; M_2 = M[2]; M_3 = M[3]; M_4 = M[4]; M_5 = M[5]; S_0 = S[0]; S_1 = S[1]; S_2 = S[2]; S_3 = S[3];
  //   S_4 = S[4]; S_5 = S[5]

  // Notes on the sheet:
  //   clk: Hz: 2
  //   PM
  //   AM
  //   Hours
  //   Minutes
  //   Set
  //   8
  //   H
  //   16
  //   32
  //   M
  //   S
  //   2
  //   4
  //   1
endmodule
