// Digital circuit computer_toy.dig as structural Verilog
module computer_toy (
  input  Load_ACC,
  input  Load_H,
  input  In_0,
  input  In_1,
  input  In_2,
  input  In_3,
  input  In_4,
  input  In_5,
  input  In_6,
  input  In_7,
  input  Load_In,
  input  Load_M,
  input  Load_L,
  input  Carry_In,
  input  X_plus_Y,
  input  X_Y,
  input  Y_X,
  input  Y_X_2,
  input  Y_X_3,
  input  Load_ROM,
  input  Load_PC_H,
  input  Load_PC_L,
  input  clk,
  input  Run,
  output [7:0] ALU,
  output [7:0] D,
  output [7:0] ACC,
  output [7:0] H,
  output [7:0] In,
  output [7:0] Bus,
  output [7:0] M,
  output [7:0] L,
  output [15:0] A,
  output [15:0] PC,
  output [7:0] ROM,
  output [7:0] PC_H,
  output [7:0] PC_L,
  output First_Cycle,
  output Zero_Bus,
  output Master_Set
);

  wire and_1_out, nm_alu_fet80_1_c_out, nm_alu_fet80_1_ng, nm_alu_fet80_1_zr, nm_clock_gen_1_clk_e,
       nm_clock_gen_1_clk_o, nm_clock_gen_1_clk_s, nm_conditionals_1_eqz, nm_conditionals_1_gez,
       nm_conditionals_1_gtz, nm_conditionals_1_lez, nm_conditionals_1_ltz, nm_conditionals_1_nez,
       nm_nand_1_out, nm_opflag_decoder_fet80_1_f, nm_opflag_decoder_fet80_1_no,
       nm_opflag_decoder_fet80_1_nx, nm_opflag_decoder_fet80_1_ny, nm_or_1_out, nm_or_2_out, nm_or_3_out,
       nm_or_4_out, nm_or_5_out, nm_or_6_out, nm_or_7_out, Save_ACC_out, Set_D_out, Set_H_out, Set_L_out,
       Set_M_out, Set_PC_H_out, Set_PC_L_out, Set_PC_out;

  and and_1 (and_1_out, clk, Run);
  nm_clock_gen nm_clock_gen_1 (
    .clk_e(nm_clock_gen_1_clk_e), .clk_s(nm_clock_gen_1_clk_s), .clk_o(nm_clock_gen_1_clk_o),
    .clk_i(and_1_out), .r(Run));
  nm_nand nm_nand_1 (.In_1(First_Cycle), .In_2(nm_clock_gen_1_clk_e), .Out(nm_nand_1_out));
  nm_tff_resetn nm_tff_resetn_1 (.T(nm_nand_1_out), .Q_2(First_Cycle), .r(Run));  // open: Q
  nm_and nm_and_1 (.In_1(nm_clock_gen_1_clk_e), .In_2(First_Cycle), .Out(Zero_Bus));
  nm_and nm_and_2 (.In_1(nm_clock_gen_1_clk_s), .In_2(First_Cycle), .Out(Master_Set));
  nm_or nm_or_1 (.Out(nm_or_1_out), .In_1(Master_Set), .In_2(Set_PC_H_out));
  Button Set_PC_H (.out(Set_PC_H_out));
  nm_or nm_or_2 (.Out(nm_or_2_out), .In_1(Master_Set), .In_2(Set_PC_L_out));
  Button Set_PC_L (.out(Set_PC_L_out));
  nm_or nm_or_3 (.Out(nm_or_3_out), .In_1(Master_Set), .In_2(Set_PC_out));
  Button Set_PC (.out(Set_PC_out));
  nm_regoc8_latch nm_regoc8_latch_1 (.D(Bus), .set(nm_or_1_out), .en(Load_PC_H), .Out(Bus), .V(PC_H));
  nm_regoc8_latch nm_regoc8_latch_2 (.D(Bus), .set(nm_or_2_out), .en(Load_PC_L), .Out(Bus), .V(PC_L));
  nm_byte2_latch nm_byte2_latch_1 (.D({PC_H, PC_L}), .set(nm_or_3_out), .Out(PC));  // open: Out_2
  ROM #(.AddrBits(16), .Bits(8)) rom_1 (.A(PC), .sel(1'b1), .D(ROM));
  nm_enableoc8 nm_enableoc8_1 (.In({In_7, In_6, In_5, In_4, In_3, In_2, In_1, In_0}), .en(Load_In), .Out(Bus));
  nm_enableoc8 nm_enableoc8_2 (.In(ROM), .en(Load_ROM), .Out(Bus));
  nm_zerooc8 nm_zerooc8_1 (.Bus(Bus), .zero(Zero_Bus));
  PullUp #(.Bits(8)) pullup_1 (.out(Bus));
  Button Set_D (.out(Set_D_out));
  nm_or nm_or_4 (.Out(nm_or_4_out), .In_1(Master_Set), .In_2(Set_D_out));
  nm_byte_latch nm_byte_latch_1 (.D(Bus), .set(nm_or_4_out), .Out(D));  // open: Out_2
  nm_ALU_FET80 nm_alu_fet80_1 (
    .X(Bus), .Y(D), .c_in(Carry_In), .Out(ALU), .zr(nm_alu_fet80_1_zr), .ng(nm_alu_fet80_1_ng),
    .c_out(nm_alu_fet80_1_c_out), .nx(nm_opflag_decoder_fet80_1_nx), .ny(nm_opflag_decoder_fet80_1_ny),
    .f(nm_opflag_decoder_fet80_1_f), .no(nm_opflag_decoder_fet80_1_no));
  nm_opflag_decoder_FET80 nm_opflag_decoder_fet80_1 (
    .nx(nm_opflag_decoder_fet80_1_nx), .ny(nm_opflag_decoder_fet80_1_ny), .f(nm_opflag_decoder_fet80_1_f),
    .no(nm_opflag_decoder_fet80_1_no), .X_plus_Y(X_plus_Y), .X_Y(X_Y), .Y_X(Y_X), .Y_X_2(Y_X_2), .Y_X_3(Y_X_3));
  LED Carry_Out (.in(nm_alu_fet80_1_c_out));
  nm_conditionals nm_conditionals_1 (
    .eqz(nm_conditionals_1_eqz), .gtz(nm_conditionals_1_gtz), .ltz(nm_conditionals_1_ltz),
    .nez(nm_conditionals_1_nez), .lez(nm_conditionals_1_lez), .gez(nm_conditionals_1_gez),
    .zr(nm_alu_fet80_1_zr), .ng(nm_alu_fet80_1_ng));
  LED gt_0 (.in(nm_conditionals_1_gtz));
  LED lt_0 (.in(nm_conditionals_1_ltz));
  LED eq_0 (.in(nm_conditionals_1_eqz));
  LED _0 (.in(nm_conditionals_1_nez));
  LED _0_2 (.in(nm_conditionals_1_lez));
  LED _0_3 (.in(nm_conditionals_1_gez));
  nm_or nm_or_5 (.Out(nm_or_5_out), .In_1(Master_Set), .In_2(Save_ACC_out));
  Button Save_ACC (.out(Save_ACC_out));
  nm_or nm_or_6 (.Out(nm_or_6_out), .In_1(Master_Set), .In_2(Set_H_out));
  Button Set_H (.out(Set_H_out));
  nm_or nm_or_7 (.Out(nm_or_7_out), .In_1(Master_Set), .In_2(Set_L_out));
  Button Set_L (.out(Set_L_out));
  nm_regoc8_latch nm_regoc8_latch_3 (.D(ALU), .set(nm_or_5_out), .en(Load_ACC), .Out(Bus), .V(ACC));
  nm_regoc8_latch nm_regoc8_latch_4 (.D(Bus), .set(nm_or_6_out), .en(Load_H), .Out(Bus), .V(A[15:8]));
  nm_regoc8_latch nm_regoc8_latch_5 (.D(Bus), .set(nm_or_7_out), .en(Load_L), .Out(Bus), .V(A[7:0]));
  Button Set_M (.out(Set_M_out));
  RAMAsync #(.AddrBits(16), .Bits(8)) ramasync_1 (.A(A), .D(Bus), .we(Set_M_out), .Q(M));
  nm_enableoc8 nm_enableoc8_3 (.In(M), .en(Load_M), .Out(Bus));

  assign H = A[15:8];
  assign In = {In_7, In_6, In_5, In_4, In_3, In_2, In_1, In_0};
  assign L = A[7:0];

  // Notes on the sheet:
  //   X_plus_Y: default 1
  //   contents of rom_1 (hex, n*v repeats v):
  //   de,ad,be,ef
endmodule
