// Digital circuit counter8.dig as structural Verilog
module counter8 (
  input  [7:0] D,
  input  clk,
  input  load,
  output [7:0] Out
);

  wire nm_and_1_out, nm_and_2_out, nm_and_3_out, nm_and_4_out, nm_and_5_out, nm_and_6_out, nm_nand_1_out,
       nm_nand_2_out, nm_nand_3_out, nm_nand_4_out, nm_nand_5_out, nm_nand_6_out, nm_nand_7_out,
       nm_nand_8_out, nm_nand_9_out, nm_nand_10_out, nm_nand_11_out, nm_nand_12_out, nm_nand_13_out,
       nm_nand_14_out, nm_nand_15_out, nm_nand_16_out, nm_not_1_out, nm_not_2_out, nm_not_3_out,
       nm_not_4_out, nm_not_5_out, nm_not_6_out, nm_not_7_out, nm_not_8_out;

  nm_nand nm_nand_1 (.In_1(D[0]), .In_2(load), .Out(nm_nand_1_out));
  tff_asyncn tff_asyncn_1 (.T(1'b1), .clk(clk), .Q(Out[0]), .r(nm_nand_2_out), .s(nm_nand_1_out));  // open: Q_2
  nm_nand nm_nand_2 (.In_1(load), .In_2(nm_not_1_out), .Out(nm_nand_2_out));
  nm_not nm_not_1 (.In(D[0]), .Out(nm_not_1_out));
  nm_nand nm_nand_3 (.In_1(D[1]), .In_2(load), .Out(nm_nand_3_out));
  tff_asyncn tff_asyncn_2 (.T(Out[0]), .clk(clk), .Q(Out[1]), .r(nm_nand_4_out), .s(nm_nand_3_out));  // open: Q_2
  nm_nand nm_nand_4 (.In_1(load), .In_2(nm_not_2_out), .Out(nm_nand_4_out));
  nm_not nm_not_2 (.In(D[1]), .Out(nm_not_2_out));
  nm_and nm_and_1 (.In_1(Out[0]), .In_2(Out[1]), .Out(nm_and_1_out));
  tff_asyncn tff_asyncn_3 (.T(nm_and_1_out), .clk(clk), .Q(Out[2]), .r(nm_nand_5_out), .s(nm_nand_6_out));  // open: Q_2
  nm_nand nm_nand_5 (.In_1(load), .In_2(nm_not_3_out), .Out(nm_nand_5_out));
  nm_nand nm_nand_6 (.In_1(D[2]), .In_2(load), .Out(nm_nand_6_out));
  nm_not nm_not_3 (.In(D[2]), .Out(nm_not_3_out));
  nm_and nm_and_2 (.In_1(nm_and_1_out), .In_2(Out[2]), .Out(nm_and_2_out));
  tff_asyncn tff_asyncn_4 (.T(nm_and_2_out), .clk(clk), .Q(Out[3]), .r(nm_nand_7_out), .s(nm_nand_8_out));  // open: Q_2
  nm_nand nm_nand_7 (.In_1(load), .In_2(nm_not_4_out), .Out(nm_nand_7_out));
  nm_nand nm_nand_8 (.In_1(D[3]), .In_2(load), .Out(nm_nand_8_out));
  nm_not nm_not_4 (.In(D[3]), .Out(nm_not_4_out));
  nm_and nm_and_3 (.In_1(nm_and_2_out), .In_2(Out[3]), .Out(nm_and_3_out));
  nm_nand nm_nand_9 (.In_1(D[4]), .In_2(load), .Out(nm_nand_9_out));
  tff_asyncn tff_asyncn_5 (
    .T(nm_and_3_out), .clk(clk), .Q(Out[4]), .r(nm_nand_10_out), .s(nm_nand_9_out));  // open: Q_2
  nm_nand nm_nand_10 (.In_1(load), .In_2(nm_not_5_out), .Out(nm_nand_10_out));
  nm_not nm_not_5 (.In(D[4]), .Out(nm_not_5_out));
  nm_and nm_and_4 (.In_1(nm_and_3_out), .In_2(Out[4]), .Out(nm_and_4_out));
  nm_nand nm_nand_11 (.In_1(D[5]), .In_2(load), .Out(nm_nand_11_out));
  tff_asyncn tff_asyncn_6 (
    .T(nm_and_4_out), .clk(clk), .Q(Out[5]), .r(nm_nand_12_out), .s(nm_nand_11_out));  // open: Q_2
  nm_nand nm_nand_12 (.In_1(load), .In_2(nm_not_6_out), .Out(nm_nand_12_out));
  nm_not nm_not_6 (.In(D[5]), .Out(nm_not_6_out));
  nm_and nm_and_5 (.In_1(nm_and_4_out), .In_2(Out[5]), .Out(nm_and_5_out));
  tff_asyncn tff_asyncn_7 (
    .T(nm_and_5_out), .clk(clk), .Q(Out[6]), .r(nm_nand_13_out), .s(nm_nand_14_out));  // open: Q_2
  nm_nand nm_nand_13 (.In_1(load), .In_2(nm_not_7_out), .Out(nm_nand_13_out));
  nm_nand nm_nand_14 (.In_1(D[6]), .In_2(load), .Out(nm_nand_14_out));
  nm_not nm_not_7 (.In(D[6]), .Out(nm_not_7_out));
  nm_and nm_and_6 (.In_1(nm_and_5_out), .In_2(Out[6]), .Out(nm_and_6_out));
  tff_asyncn tff_asyncn_8 (
    .T(nm_and_6_out), .clk(clk), .Q(Out[7]), .r(nm_nand_15_out), .s(nm_nand_16_out));  // open: Q_2
  nm_nand nm_nand_15 (.In_1(load), .In_2(nm_not_8_out), .Out(nm_nand_15_out));
  nm_nand nm_nand_16 (.In_1(D[7]), .In_2(load), .Out(nm_nand_16_out));
  nm_not nm_not_8 (.In(D[7]), .Out(nm_not_8_out));
endmodule
