// Digital circuit nc_p3.dig as structural Verilog
module nc_p3 (
  input  In_1,
  input  In_2,
  input  In_3,
  input  D,
  input  S
);

  NFET nfet_1 (.G(In_1), .D(D), .S(S));
  NFET nfet_2 (.G(In_2), .D(D), .S(S));
  NFET nfet_3 (.G(In_3), .D(D), .S(S));
endmodule
