// Digital circuit nc_s4.dig as structural Verilog
module nc_s4 (
  input  In_1,
  input  In_2,
  input  In_3,
  input  In_4,
  input  D,
  input  S
);

  wire nfet_1_s, nfet_2_s, nfet_3_s;

  NFET nfet_1 (.G(In_1), .D(D), .S(nfet_1_s));
  NFET nfet_2 (.G(In_2), .D(nfet_1_s), .S(nfet_2_s));
  NFET nfet_3 (.G(In_3), .D(nfet_2_s), .S(nfet_3_s));
  NFET nfet_4 (.G(In_4), .D(nfet_3_s), .S(S));
endmodule
