// Digital circuit nm_7seg.dig as structural Verilog
module nm_7seg (
  input  [3:0] In,
  output a,
  output b,
  output c,
  output d,
  output e,
  output f,
  output g
);

  wire In_A_t, In_B_t, In_C_t, in_D_t, nm_aoi3_3_3_3_2_1_out, nm_nand3_1_out, nm_nand3_2_out, nm_nand3_3_out,
       nm_nand3_4_out, nm_nand3_5_out, nm_nand3_6_out, nm_nand_1_out, nm_nand_2_out, nm_nand_3_out,
       nm_nand_4_out, nm_nand_5_out, nm_nand_6_out, nm_nand_7_out, nm_nand_8_out, nm_nand_9_out,
       nm_nand_10_out, nm_nand_11_out, nm_nand_12_out, nm_nand_13_out, nm_nand_14_out, nm_nand_15_out,
       nm_nand_16_out, nm_nand_17_out;

  nm_nand nm_nand_1 (.In_1(In[0]), .In_2(In[3]), .Out(nm_nand_1_out));
  nm_nand nm_nand_2 (.In_1(In[1]), .In_2(In_B_t), .Out(nm_nand_2_out));
  nm_nand3 nm_nand3_1 (.In_1(In_C_t), .In_2(In[2]), .In_3(In_A_t), .Out(nm_nand3_1_out));
  nm_nand nm_nand_3 (.In_1(in_D_t), .In_2(In[2]), .Out(nm_nand_3_out));
  nm_nand nm_nand_4 (.In_1(in_D_t), .In_2(In_C_t), .Out(nm_nand_4_out));
  nm_nand nm_nand_5 (.In_1(In[2]), .In_2(In[3]), .Out(nm_nand_5_out));
  nm_nand nm_nand_6 (.In_1(In[1]), .In_2(In[3]), .Out(nm_nand_6_out));
  nm_nand nm_nand_7 (.In_1(in_D_t), .In_2(In[1]), .Out(nm_nand_7_out));
  nm_not nm_not_1 (.In(nm_aoi3_3_3_3_2_1_out), .Out(d));
  nm_aoi3_3_3_3_2 nm_aoi3_3_3_3_2_1 (
    .Out(nm_aoi3_3_3_3_2_1_out), .In_A1(in_D_t), .In_A2(In_B_t), .In_A3(In_A_t), .In_B1(In[0]),
    .In_B2(In[1]), .In_B3(In_B_t), .In_C1(In[0]), .In_C2(In_C_t), .In_C3(In[2]), .In_D1(in_D_t),
    .In_D2(In[1]), .In_D3(In[2]), .In_E1(In_C_t), .In_E2(In[3]));
  nm_nand nm_nand_8 (.In_1(In_B_t), .In_2(In[3]), .Out(nm_nand_8_out));
  nm_nand nm_nand_9 (.In_1(In[2]), .In_2(In_A_t), .Out(nm_nand_9_out));
  nm_nand nm_nand_10 (.In_1(In[0]), .In_2(In_C_t), .Out(nm_nand_10_out));
  nm_nand nm_nand_11 (.In_1(In[0]), .In_2(In_A_t), .Out(nm_nand_11_out));
  nm_nand nm_nand_12 (.In_1(In_C_t), .In_2(In_A_t), .Out(nm_nand_12_out));
  nm_nand3 nm_nand3_2 (.In_1(In[0]), .In_2(In_C_t), .In_3(In[3]), .Out(nm_nand3_2_out));
  nm_nand3 nm_nand3_3 (.In_1(In[0]), .In_2(In[1]), .In_3(In_A_t), .Out(nm_nand3_3_out));
  nm_nand3 nm_nand3_4 (.In_1(in_D_t), .In_2(In_C_t), .In_3(In_A_t), .Out(nm_nand3_4_out));
  nm_nand nm_nand_13 (.In_1(In_B_t), .In_2(In_A_t), .Out(nm_nand_13_out));
  nm_nand3 nm_nand3_5 (.In_1(In_C_t), .In_2(In_B_t), .In_3(In[3]), .Out(nm_nand3_5_out));
  nm_nand3 nm_nand3_6 (.In_1(In[0]), .In_2(In[2]), .In_3(In_A_t), .Out(nm_nand3_6_out));
  nm_nand nm_nand_14 (.In_1(in_D_t), .In_2(In[3]), .Out(nm_nand_14_out));
  nm_nand nm_nand_15 (.In_1(In[1]), .In_2(In[2]), .Out(nm_nand_15_out));
  nm_nand nm_nand_16 (.In_1(In[1]), .In_2(In_A_t), .Out(nm_nand_16_out));
  nm_nand nm_nand_17 (.In_1(in_D_t), .In_2(In_B_t), .Out(nm_nand_17_out));
  // nm_not nm_not_2: pin names not known; wires that end beside it: In[3], In_A_t, In[2], In_B_t, In[1], In_C_t, In[0], in_D_t, In_A_t, In[3]
  nm_not nm_not_3 (.In(In[2]), .Out(In_B_t));
  nm_not nm_not_4 (.In(In[1]), .Out(In_C_t));
  nm_nand6 nm_nand6_1 (
    .In_1(nm_nand_17_out), .In_2(nm_nand_16_out), .In_3(nm_nand_15_out), .In_4(nm_nand_14_out),
    .In_5(nm_nand3_6_out), .In_6(nm_nand3_5_out), .Out(a));
  nm_nand5 nm_nand5_1 (
    .In_1(nm_nand_13_out), .In_2(nm_nand_17_out), .In_3(nm_nand3_4_out), .In_4(nm_nand3_3_out),
    .In_5(nm_nand3_2_out), .Out(b));
  nm_nand5 nm_nand5_2 (
    .In_1(nm_nand_12_out), .In_2(nm_nand_11_out), .In_3(nm_nand_10_out), .In_4(nm_nand_9_out),
    .In_5(nm_nand_8_out), .Out(c));
  nm_nand4 nm_nand4_1 (
    .In_1(nm_nand_17_out), .In_2(nm_nand_7_out), .In_3(nm_nand_6_out), .In_4(nm_nand_5_out), .Out(e));
  nm_nand5 nm_nand5_3 (
    .In_1(nm_nand_4_out), .In_2(nm_nand_3_out), .In_3(nm_nand_8_out), .In_4(nm_nand_6_out),
    .In_5(nm_nand3_1_out), .Out(f));
  nm_nand5 nm_nand5_4 (
    .In_1(nm_nand_2_out), .In_2(nm_nand_7_out), .In_3(nm_nand_8_out), .In_4(nm_nand_1_out),
    .In_5(nm_nand3_1_out), .Out(g));
  nm_not nm_not_5 (.In(In[0]), .Out(in_D_t));

  // Other names for the same wires on the sheet: in_D = In[0]; In_C = In[1]; In_B = In[2]; In_A = In[3]

  // Notes on the sheet:
  //   Products Stage
  //   AD
  //   B'C
  //   A'BC'
  //   BD'
  //   C'D'
  //   AB
  //   AC
  //   CD'
  //   AC'
  //   BCD'
  //   BC'D
  //   B'CD
  //   A'B'D'
  //   AB'
  //   A'B
  //   C'D
  //   A'D
  //   A'C'
  //   AC'D
  //   A'CD
  //   A'C'D'
  //   A'B'
  //   AB'C'
  //   A'BD
  //   AD'
  //   BC
  //   A'C
  //   B'D'
  //   Sum Stage
  //   a = B'D' + A'C + BC + AD' + A'BD + AB'C'
  //   b = A'B' + B'D' + A'C'D' + A'CD + AC'D
  //   c = A'C' + A'D + C'D + A'B + AB'
  //   d = AC' + A'B'D' + B'CD + BC'D + BCD'
  //   e = B'D' + CD' + AC + AB
  //   f = C'D' + BD' + AB' + AC + A'BC'
  //   g = B'C + CD' + AB' + AD + A'BC'
endmodule
