// Digital circuit nm_ALU_FET80.dig as structural Verilog
module nm_ALU_FET80 (
  input  [7:0] X,
  input  [7:0] Y,
  input  nx,
  input  ny,
  input  f,
  input  c_in,
  input  no,
  output [7:0] Out,
  output c_out
);

  wire [7:0] nm_adder8_1_and, nm_adder8_1_sum, nm_inverter8_1_out, nm_inverter8_2_out, nm_muxn8_1_out;

  nm_inverter8 nm_inverter8_1 (.In(X), .inv(nx), .Out(nm_inverter8_1_out));
  nm_inverter8 nm_inverter8_2 (.In(Y), .inv(ny), .Out(nm_inverter8_2_out));
  nm_adder8 nm_adder8_1 (
    .A(nm_inverter8_1_out), .B(nm_inverter8_2_out), .sum(nm_adder8_1_sum), .c_in(c_in), .c_out(c_out),
    .\and (nm_adder8_1_and));  // open: xor
  nm_muxn8 nm_muxn8_1 (.A(nm_adder8_1_and), .B(nm_adder8_1_sum), .s(f), .Out(nm_muxn8_1_out));
  nm_invertern8 nm_invertern8_1 (.In(nm_muxn8_1_out), .inv(no), .Out(Out));
endmodule

/* Test case:
nx ny f no   X Y   Out

# ADD
loop(a,64)
  loop(b, 64)
  0 0 1 0  (a) (b)  (a+b)
  end loop
end loop

# SUB
loop(a,64)
  loop(b, 64)
  1 0 1 1  (a) (b)  (a-b)
  end loop
end loop

# SUBR
loop(a,64)
  loop(b, 64)
  0 1 1 1  (a) (b)  (b-a)
  end loop
end loop

# AND
loop(a,256)
  loop(b, 256)
  0 0 0 0  (a) (b)  (a&b)
  end loop
end loop

# NAND
loop(a,256)
  loop(b, 256)
  0 0 0 1  (a) (b)  (~(a&b))
  end loop
end loop

# OR
loop(a,256)
  loop(b, 256)
  1 1 0 1  (a) (b)  (a|b)
  end loop
end loop

# NOR
loop(a,256)
  loop(b, 256)
  1 1 0 0  (a) (b)  (~(a|b))
  end loop
end loop
*/
