// Digital circuit nm_AOI2-1.dig as structural Verilog
module nm_AOI2_1 (
  input  In_1,
  input  In_2,
  input  In_3,
  output Out
);

  wire nfet_1_s;

  NFET nfet_1 (.G(In_1), .D(Out), .S(nfet_1_s));
  NFET nfet_2 (.G(In_2), .D(nfet_1_s), .S(1'b0));
  PullUp pullup_1 (.out(Out));
  NFET nfet_3 (.G(In_3), .D(Out), .S(1'b0));
endmodule

/* Test case:
In_1 In_2 In_3 Out

repeat(4) bits(2,n) 1 0

0 0 0 1
0 1 0 1
1 0 0 1
1 1 0 0
*/
