// Digital circuit nm_AOI2-2-4.dig as structural Verilog
module nm_AOI2_2_4 (
  input  In_1,
  input  In_2,
  input  In_3,
  input  In_4,
  input  In_5,
  input  In_6,
  input  In_7,
  input  In_8,
  output Out
);

  wire nfet_1_s, nfet_3_s, nfet_5_s, nfet_7_s;

  NFET nfet_1 (.G(In_1), .D(Out), .S(nfet_1_s));
  NFET nfet_2 (.G(In_2), .D(nfet_1_s), .S(1'b0));
  PullUp pullup_1 (.out(Out));
  NFET nfet_3 (.G(In_3), .D(Out), .S(nfet_3_s));
  NFET nfet_4 (.G(In_4), .D(nfet_3_s), .S(1'b0));
  NFET nfet_5 (.G(In_5), .D(Out), .S(nfet_5_s));
  NFET nfet_6 (.G(In_6), .D(nfet_5_s), .S(1'b0));
  NFET nfet_7 (.G(In_7), .D(Out), .S(nfet_7_s));
  NFET nfet_8 (.G(In_8), .D(nfet_7_s), .S(1'b0));
endmodule

/* Test case:
# Not full coverage

In_1 In_2 In_3 In_4 Out

loop(x, 3)
	loop(y, 3)
		bits(2,x) bits(2,y) 1
	end loop
end loop

loop(x, 4)
	bits(2,x) 1 1 0
end loop

loop(y, 4)
	1 1 bits(2,y) 0
end loop
*/
