// Digital circuit nm_AOI2-2.dig as structural Verilog
module nm_AOI2_2 (
  input  In_1,
  input  In_2,
  input  In_3,
  input  In_4,
  output Out
);

  wire nfet_1_s, nfet_3_s;

  NFET nfet_1 (.G(In_1), .D(Out), .S(nfet_1_s));
  NFET nfet_2 (.G(In_2), .D(nfet_1_s), .S(1'b0));
  PullUp pullup_1 (.out(Out));
  NFET nfet_3 (.G(In_3), .D(Out), .S(nfet_3_s));
  NFET nfet_4 (.G(In_4), .D(nfet_3_s), .S(1'b0));
endmodule

/* Test case:
In_1 In_2 In_3 In_4 Out

loop(x, 3)
	loop(y, 3)
		bits(2,x) bits(2,y) 1
	end loop
end loop

loop(x, 4)
	bits(2,x) 1 1 0
end loop

loop(y, 4)
	1 1 bits(2,y) 0
end loop
*/
