// Digital circuit nm_And.dig as structural Verilog
module nm_And (
  input  In_1,
  input  In_2,
  output Out
);

  wire nm_nand_1_out;

  nm_Nand nm_nand_1 (.In_1(In_1), .In_2(In_2), .Out(nm_nand_1_out));
  nm_Not nm_not_1 (.In(nm_nand_1_out), .Out(Out));
endmodule

/* Test case:
In_1 In_2 Out

0 0 0
0 1 0
1 0 0
1 1 1
*/
