// Digital circuit nm_And8x.dig as structural Verilog
module nm_And8x (
  input  [7:0] In_1,
  input  [7:0] In_2,
  output [7:0] Out
);

  nm_And nm_and_1 (.Out(Out[0]), .In_1(In_1[0]), .In_2(In_2[0]));
  nm_And nm_and_2 (.Out(Out[1]), .In_1(In_1[1]), .In_2(In_2[1]));
  nm_And nm_and_3 (.Out(Out[2]), .In_1(In_1[2]), .In_2(In_2[2]));
  nm_And nm_and_4 (.Out(Out[3]), .In_1(In_1[3]), .In_2(In_2[3]));
  nm_And nm_and_5 (.Out(Out[4]), .In_1(In_1[4]), .In_2(In_2[4]));
  nm_And nm_and_6 (.Out(Out[5]), .In_1(In_1[5]), .In_2(In_2[5]));
  nm_And nm_and_7 (.Out(Out[6]), .In_1(In_1[6]), .In_2(In_2[6]));
  nm_And nm_and_8 (.Out(Out[7]), .In_1(In_1[7]), .In_2(In_2[7]));
endmodule
