// Digital circuit nm_Counter16.dig as structural Verilog
module nm_Counter16 (
  input  [15:0] D,
  input  clk,
  input  set,
  input  reset,
  output [15:0] Out
);

  wire notconnected_1_out;
  wire [15:0] nm_fulladder16_1_sum, nm_mux16_1_out;

  // NotConnected on notconnected_1_out
  nm_FullAdder16 nm_fulladder16_1 (
    .A(Out), .B(16'h1), .c_in(notconnected_1_out), .sum(nm_fulladder16_1_sum));  // open: c_out
  nm_mux16 nm_mux16_1 (.A(nm_fulladder16_1_sum), .s(set), .B(D), .Out(nm_mux16_1_out));
  nm_byte2 nm_byte2_1 (.D(nm_mux16_1_out), .clk(clk), .reset(reset), .Out(Out));
endmodule
