// Digital circuit nm_DFF.dig as structural Verilog
module nm_DFF (
  input  D,
  input  clk,
  input  r,
  output Q,
  output Q_2
);

  wire delay_1_out, nm_nand3_1_out, nm_nand3_2_out, nm_nand3_3_out, nm_nand_1_out, nm_not_1_out;

  Delay delay_1 (.in(D), .out(delay_1_out));
  nm_Not nm_not_1 (.In(r), .Out(nm_not_1_out));
  nm_Nand nm_nand_1 (.In_1(nm_nand3_3_out), .In_2(nm_nand3_1_out), .Out(nm_nand_1_out));
  nm_Nand3 nm_nand3_1 (.In_1(nm_nand_1_out), .In_2(clk), .In_3(nm_not_1_out), .Out(nm_nand3_1_out));
  nm_Nand3 nm_nand3_2 (.In_1(nm_nand3_1_out), .In_2(clk), .In_3(nm_nand3_3_out), .Out(nm_nand3_2_out));
  nm_Nand3 nm_nand3_3 (.In_1(nm_nand3_2_out), .In_2(delay_1_out), .In_3(nm_not_1_out), .Out(nm_nand3_3_out));
  nm_Nand nm_nand_2 (.In_1(nm_nand3_1_out), .In_2(Q_2), .Out(Q));
  nm_Nand3 nm_nand3_4 (.In_1(Q), .In_2(nm_nand3_2_out), .In_3(nm_not_1_out), .Out(Q_2));
endmodule

/* Test case:
r clk D Q

1 0 0 0

0 1 0 0
0 0 1 0
0 1 1 1
0 0 0 1
0 1 0 0
0 0 0 0
0 1 0 0
0 0 1 0
0 1 1 1
0 0 1 1
0 1 1 1
0 0 0 1
0 1 0 0
0 0 1 0
0 1 1 1
0 0 0 1

# A real DFF works, but the
# Logic simulator oscilates here
#0 1 0 0
#0 0 1 0
#0 1 0 0
#0 0 0 0
#0 1 0 0
#0 0 0 0
#0 1 0 0
#0 0 0 0
#0 1 1 1
#0 0 1 1
#0 1 0 0
#0 0 1 0
#0 1 1 1
#0 0 0 1
#0 1 1 1
#0 0 0 1
*/
