// Digital circuit nm_FullAdder.dig as structural Verilog
module nm_FullAdder (
  input  A,
  input  B,
  input  c_in,
  output sum,
  output c_out
);

  wire nm_halfadder_1_carry, nm_halfadder_1_sum, nm_halfadder_2_carry;

  nm_HalfAdder nm_halfadder_1 (.A(A), .B(B), .sum(nm_halfadder_1_sum), .carry(nm_halfadder_1_carry));
  nm_HalfAdder nm_halfadder_2 (.A(nm_halfadder_1_sum), .B(c_in), .sum(sum), .carry(nm_halfadder_2_carry));
  nm_Or nm_or_1 (.In_1(nm_halfadder_2_carry), .In_2(nm_halfadder_1_carry), .Out(c_out));
endmodule
