// Digital circuit nm_FullAdder16.dig as structural Verilog
module nm_FullAdder16 (
  input  [15:0] A,
  input  [15:0] B,
  input  c_in,
  output [15:0] sum,
  output c_out
);

  wire nm_fulladder8_1_c_out;

  nm_FullAdder8 nm_fulladder8_1 (.A(A[7:0]), .B(B[7:0]), .c_in(c_in), .sum(sum[7:0]), .c_out(nm_fulladder8_1_c_out));
  nm_FullAdder8 nm_fulladder8_2 (
    .A(A[15:8]), .B(B[15:8]), .c_in(nm_fulladder8_1_c_out), .sum(sum[15:8]), .c_out(c_out));
endmodule
