// Digital circuit nm_FullAdder8.dig as structural Verilog
module nm_FullAdder8 (
  input  [7:0] A,
  input  [7:0] B,
  input  c_in,
  output [7:0] sum,
  output c_out
);

  wire nm_fulladder_1_c_out, nm_fulladder_2_c_out, nm_fulladder_3_c_out, nm_fulladder_4_c_out,
       nm_fulladder_5_c_out, nm_fulladder_6_c_out, nm_fulladder_7_c_out;

  nm_FullAdder nm_fulladder_1 (.A(A[0]), .B(B[0]), .c_in(c_in), .sum(sum[0]), .c_out(nm_fulladder_1_c_out));
  nm_FullAdder nm_fulladder_2 (
    .A(A[1]), .B(B[1]), .c_in(nm_fulladder_1_c_out), .sum(sum[1]), .c_out(nm_fulladder_2_c_out));
  nm_FullAdder nm_fulladder_3 (
    .A(A[2]), .B(B[2]), .c_in(nm_fulladder_2_c_out), .sum(sum[2]), .c_out(nm_fulladder_3_c_out));
  nm_FullAdder nm_fulladder_4 (
    .A(A[3]), .B(B[3]), .c_in(nm_fulladder_3_c_out), .sum(sum[3]), .c_out(nm_fulladder_4_c_out));
  nm_FullAdder nm_fulladder_5 (
    .A(A[4]), .B(B[4]), .c_in(nm_fulladder_4_c_out), .sum(sum[4]), .c_out(nm_fulladder_5_c_out));
  nm_FullAdder nm_fulladder_6 (
    .A(A[5]), .B(B[5]), .c_in(nm_fulladder_5_c_out), .sum(sum[5]), .c_out(nm_fulladder_6_c_out));
  nm_FullAdder nm_fulladder_7 (
    .A(A[6]), .B(B[6]), .c_in(nm_fulladder_6_c_out), .sum(sum[6]), .c_out(nm_fulladder_7_c_out));
  nm_FullAdder nm_fulladder_8 (.A(A[7]), .B(B[7]), .c_in(nm_fulladder_7_c_out), .sum(sum[7]), .c_out(c_out));
endmodule
