// Digital circuit nm_HACK_opflag_decoder.dig as structural Verilog
module nm_HACK_opflag_decoder (
  input  _0,
  input  _1,
  input  _1_2,
  input  X,
  input  Y,
  input  X_2,
  input  Y_2,
  input  X_3,
  input  Y_3,
  input  X_plus_1,
  input  Y_plus_1,
  input  X_1,
  input  Y_1,
  input  X_plus_Y,
  input  X_Y,
  input  Y_X,
  input  Y_X_2,
  input  Y_X_3,
  output zx,
  output nx,
  output zy,
  output ny,
  output f,
  output no
);

  nm_or8 nm_or8_1 (
    .Out(zx), .In_1(_0), .In_2(_1), .In_3(_1_2), .In_4(Y), .In_5(Y_2), .In_6(Y_3), .In_7(Y_plus_1), .In_8(Y_1));
  nm_nor8 nm_nor8_1 (
    .Out(nx), .In_1(_0), .In_2(X), .In_3(X_2), .In_4(X_3), .In_5(X_1), .In_6(X_plus_Y), .In_7(Y_X),
    .In_8(Y_X_2));
  nm_or8 nm_or8_2 (
    .Out(zy), .In_1(_0), .In_2(_1), .In_3(_1_2), .In_4(X), .In_5(X_2), .In_6(X_3), .In_7(X_plus_1), .In_8(X_1));
  nm_nor9 nm_nor9_1 (
    .In_1(_0), .In_2(_1_2), .In_3(Y), .In_4(Y_2), .In_5(Y_3), .In_6(Y_1), .In_7(X_plus_Y), .In_8(X_Y),
    .In_9(Y_X_2), .Out(ny));
  nm_nor6 nm_nor6_1 (.Out(f), .In_1(X), .In_2(Y), .In_3(X_2), .In_4(Y_2), .In_5(Y_X_2), .In_6(Y_X_3));
  nm_nor8 nm_nor8_2 (
    .Out(no), .In_1(_0), .In_2(_1_2), .In_3(X), .In_4(Y), .In_5(X_1), .In_6(Y_1), .In_7(X_plus_Y),
    .In_8(Y_X_2));
endmodule
