// Digital circuit nm_HalfAdder.dig as structural Verilog
module nm_HalfAdder (
  input  A,
  input  B,
  output sum,
  output carry
);

  nm_Xor nm_xor_1 (.In_1(A), .In_2(B), .Out(sum));
  nm_And nm_and_1 (.In_1(A), .In_2(B), .Out(carry));
endmodule
