// Digital circuit nm_Inverter8.dig as structural Verilog
module nm_Inverter8 (
  input  [7:0] In,
  input  inv,
  output [7:0] Out
);

  nm_Xor nm_xor_1 (.In_1(In[0]), .In_2(inv), .Out(Out[0]));
  nm_Xor nm_xor_2 (.In_1(In[1]), .In_2(inv), .Out(Out[1]));
  nm_Xor nm_xor_3 (.In_1(In[2]), .In_2(inv), .Out(Out[2]));
  nm_Xor nm_xor_4 (.In_1(In[3]), .In_2(inv), .Out(Out[3]));
  nm_Xor nm_xor_5 (.In_1(In[4]), .In_2(inv), .Out(Out[4]));
  nm_Xor nm_xor_6 (.In_1(In[5]), .In_2(inv), .Out(Out[5]));
  nm_Xor nm_xor_7 (.In_1(In[6]), .In_2(inv), .Out(Out[6]));
  nm_Xor nm_xor_8 (.In_1(In[7]), .In_2(inv), .Out(Out[7]));
endmodule
