// Digital circuit nm_Nand.dig as structural Verilog
module nm_Nand (
  input  In_1,
  input  In_2,
  output Out
);

  wire nfet_1_s;

  NFET nfet_1 (.G(In_1), .D(Out), .S(nfet_1_s));
  NFET nfet_2 (.G(In_2), .D(nfet_1_s), .S(1'b0));
  PullUp pullup_1 (.out(Out));
endmodule
