// Digital circuit nm_Nor.dig as structural Verilog
module nm_Nor (
  input  In_1,
  input  In_2,
  output Out
);

  NFET nfet_1 (.G(In_1), .D(Out), .S(1'b0));
  PullUp pullup_1 (.out(Out));
  NFET nfet_2 (.G(In_2), .D(Out), .S(1'b0));
endmodule
