// Digital circuit nm_Nor10.dig as structural Verilog
module nm_Nor10 (
  input  In_1,
  input  In_2,
  input  In_3,
  input  In_4,
  input  In_5,
  input  In_6,
  input  In_7,
  input  In_8,
  input  In_9,
  input  In_10,
  output Out
);

  NFET nfet_1 (.G(In_1), .D(Out), .S(1'b0));
  PullUp pullup_1 (.out(Out));
  NFET nfet_2 (.G(In_2), .D(Out), .S(1'b0));
  NFET nfet_3 (.G(In_3), .D(Out), .S(1'b0));
  NFET nfet_4 (.G(In_4), .D(Out), .S(1'b0));
  NFET nfet_5 (.G(In_5), .D(Out), .S(1'b0));
  NFET nfet_6 (.G(In_6), .D(Out), .S(1'b0));
  NFET nfet_7 (.G(In_7), .D(Out), .S(1'b0));
  NFET nfet_8 (.G(In_8), .D(Out), .S(1'b0));
  NFET nfet_9 (.G(In_9), .D(Out), .S(1'b0));
  NFET nfet_10 (.G(In_10), .D(Out), .S(1'b0));
endmodule
