// Digital circuit nm_Or10.dig as structural Verilog
module nm_Or10 (
  input  In_1,
  input  In_2,
  input  In_3,
  input  In_4,
  input  In_5,
  input  In_6,
  input  In_7,
  input  In_8,
  input  In_9,
  input  In_10,
  output Out
);

  wire nm_nor10_1_out;

  nm_Nor10 nm_nor10_1 (
    .Out(nm_nor10_1_out), .In_1(In_1), .In_2(In_2), .In_3(In_3), .In_4(In_4), .In_5(In_5), .In_6(In_6),
    .In_7(In_7), .In_8(In_8), .In_9(In_9), .In_10(In_10));
  nm_Not nm_not_1 (.In(nm_nor10_1_out), .Out(Out));
endmodule
