// Digital circuit nm_Reg8.dig as structural Verilog
module nm_Reg8 (
  input  [7:0] D,
  input  clk,
  input  reset,
  input  en,
  output [7:0] Out,
  output [7:0] V
);

  nm_Bit nm_bit_1 (.D(D[0]), .clk(clk), .en(en), .reset(reset), .Out(Out[0]), .V(V[0]));
  nm_Bit nm_bit_2 (.D(D[1]), .clk(clk), .en(en), .reset(reset), .Out(Out[1]), .V(V[1]));
  nm_Bit nm_bit_3 (.D(D[2]), .clk(clk), .en(en), .reset(reset), .Out(Out[2]), .V(V[2]));
  nm_Bit nm_bit_4 (.D(D[3]), .clk(clk), .en(en), .reset(reset), .Out(Out[3]), .V(V[3]));
  nm_Bit nm_bit_5 (.D(D[4]), .clk(clk), .en(en), .reset(reset), .Out(Out[4]), .V(V[4]));
  nm_Bit nm_bit_6 (.D(D[5]), .clk(clk), .en(en), .reset(reset), .Out(Out[5]), .V(V[5]));
  nm_Bit nm_bit_7 (.D(D[6]), .clk(clk), .en(en), .reset(reset), .Out(Out[6]), .V(V[6]));
  nm_Bit nm_bit_8 (.D(D[7]), .clk(clk), .en(en), .reset(reset), .Out(Out[7]), .V(V[7]));
endmodule
