// Digital circuit nm_Xor.dig as structural Verilog
module nm_Xor (
  input  In_1,
  input  In_2,
  output Out
);

  wire nfet_1_s, nfet_3_s, nm_not_1_out, nm_not_2_out;

  NFET nfet_1 (.G(In_1), .D(Out), .S(nfet_1_s));
  NFET nfet_2 (.G(In_2), .D(nfet_1_s), .S(1'b0));
  PullUp pullup_1 (.out(Out));
  nm_Not nm_not_1 (.In(In_1), .Out(nm_not_1_out));
  nm_Not nm_not_2 (.In(In_2), .Out(nm_not_2_out));
  NFET nfet_3 (.G(nm_not_1_out), .D(Out), .S(nfet_3_s));
  NFET nfet_4 (.G(nm_not_2_out), .D(nfet_3_s), .S(1'b0));
endmodule
