// Digital circuit nm_adder+.dig as structural Verilog
module nm_adder (
  input  A,
  input  B,
  input  c_in,
  output sum,
  output c_out,
  output \xor ,
  output \nand ,
  output \and ,
  output \nor 
);

  wire nm_halfadder_2_carry;

  nm_halfadder nm_halfadder_1 (.A(A), .B(B), .sum(\xor ), .carry(\and ), .\nand (\nand ), .\nor (\nor ));
  nm_halfadder nm_halfadder_2 (.A(\xor ), .B(c_in), .sum(sum), .carry(nm_halfadder_2_carry));
  nm_or nm_or_1 (.In_1(nm_halfadder_2_carry), .In_2(\and ), .Out(c_out));
endmodule
