// Digital circuit nm_adder4+.dig as structural Verilog
module nm_adder4 (
  input  [3:0] A,
  input  [3:0] B,
  input  c_in,
  output [3:0] sum,
  output c_out,
  output [3:0] \nand ,
  output [3:0] \nor ,
  output [3:0] \and ,
  output [3:0] \xor 
);

  wire nm_adder_1_c_out, nm_adder_2_c_out, nm_adder_3_c_out;

  nm_adder nm_adder_1 (
    .A(A[0]), .B(B[0]), .c_in(c_in), .sum(sum[0]), .c_out(nm_adder_1_c_out), .\xor (\xor [0]),
    .\and (\and [0]), .\nor (\nor [0]), .\nand (\nand [0]));
  nm_adder nm_adder_2 (
    .A(A[1]), .B(B[1]), .c_in(nm_adder_1_c_out), .sum(sum[1]), .c_out(nm_adder_2_c_out), .\xor (\xor [1]),
    .\and (\and [1]), .\nor (\nor [1]), .\nand (\nand [1]));
  nm_adder nm_adder_3 (
    .A(A[2]), .B(B[2]), .c_in(nm_adder_2_c_out), .sum(sum[2]), .c_out(nm_adder_3_c_out), .\xor (\xor [2]),
    .\and (\and [2]), .\nor (\nor [2]), .\nand (\nand [2]));
  nm_adder nm_adder_4 (
    .A(A[3]), .B(B[3]), .c_in(nm_adder_3_c_out), .sum(sum[3]), .c_out(c_out), .\xor (\xor [3]),
    .\and (\and [3]), .\nor (\nor [3]), .\nand (\nand [3]));

  // Other names for the same wires on the sheet: and_0 = \and [0]; and_1 = \and [1]; and_2 = \and [2];
  //   and_3 = \and [3]; nand_0 = \nand [0]; nand_1 = \nand [1]; nand_2 = \nand [2]; nand_3 = \nand [3];
  //   nor_0 = \nor [0]; nor_1 = \nor [1]; nor_2 = \nor [2]; nor_3 = \nor [3]; xor_0 = \xor [0]; xor_1 = \xor [1];
  //   xor_2 = \xor [2]; xor_3 = \xor [3]
endmodule
