// Digital circuit nm_adder_nand.dig as structural Verilog
module nm_adder_nand (
  input  A,
  input  B,
  output sum,
  output carry,
  output \nand 
);

  nm_xor nm_xor_1 (.In_1(A), .In_2(B), .Out(sum));
  nm_and nm_and_1 (.Out(carry), .In_1(A), .In_2(B), .Out_2(\nand ));
endmodule
