// Digital circuit nm_aoi2x2x2x2.dig as structural Verilog
module nm_aoi2x2x2x2 (
  input  In_A1,
  input  In_A2,
  input  In_B1,
  input  In_B2,
  input  In_C1,
  input  In_C2,
  input  In_D1,
  input  In_D2,
  output Out
);

  wire nfet_1_s, nfet_3_s, nfet_5_s, nfet_7_s;

  NFET nfet_1 (.G(In_A1), .D(Out), .S(nfet_1_s));
  NFET nfet_2 (.G(In_A2), .D(nfet_1_s), .S(1'b0));
  PullUp pullup_1 (.out(Out));
  NFET nfet_3 (.G(In_B1), .D(Out), .S(nfet_3_s));
  NFET nfet_4 (.G(In_B2), .D(nfet_3_s), .S(1'b0));
  NFET nfet_5 (.G(In_C1), .D(Out), .S(nfet_5_s));
  NFET nfet_6 (.G(In_C2), .D(nfet_5_s), .S(1'b0));
  NFET nfet_7 (.G(In_D1), .D(Out), .S(nfet_7_s));
  NFET nfet_8 (.G(In_D2), .D(nfet_7_s), .S(1'b0));
endmodule
