// Digital circuit nm_byte.dig as structural Verilog
module nm_byte (
  input  [7:0] D,
  input  clk,
  input  reset,
  output [7:0] Out
);

  nm_dff nm_dff_1 (.D(D[0]), .clk(clk), .r(reset), .Q(Out[0]));  // open: Q_2
  nm_dff nm_dff_2 (.D(D[1]), .clk(clk), .r(reset), .Q(Out[1]));  // open: Q_2
  nm_dff nm_dff_3 (.D(D[2]), .clk(clk), .r(reset), .Q(Out[2]));  // open: Q_2
  nm_dff nm_dff_4 (.D(D[3]), .clk(clk), .r(reset), .Q(Out[3]));  // open: Q_2
  nm_dff nm_dff_5 (.D(D[4]), .clk(clk), .r(reset), .Q(Out[4]));  // open: Q_2
  nm_dff nm_dff_6 (.D(D[5]), .clk(clk), .r(reset), .Q(Out[5]));  // open: Q_2
  nm_dff nm_dff_7 (.D(D[6]), .clk(clk), .r(reset), .Q(Out[6]));  // open: Q_2
  nm_dff nm_dff_8 (.D(D[7]), .clk(clk), .r(reset), .Q(Out[7]));  // open: Q_2
endmodule
