// Digital circuit nm_byte2_latch.dig as structural Verilog
module nm_byte2_latch (
  input  [15:0] D,
  input  set,
  output [15:0] Out,
  output [15:0] Out_2
);

  nm_byte_latch nm_byte_latch_1 (.D(D[7:0]), .set(set), .Out(Out[7:0]), .Out_2(Out_2[7:0]));
  nm_byte_latch nm_byte_latch_2 (.D(D[15:8]), .set(set), .Out(Out[15:8]), .Out_2(Out_2[15:8]));
endmodule
