// Digital circuit nm_byte_latch.dig as structural Verilog
module nm_byte_latch (
  input  [7:0] D,
  input  set,
  output [7:0] Out,
  output [7:0] Out_2
);

  nm_d_gated nm_d_gated_1 (.D(D[0]), .E(set), .Q(Out[0]), .Q_2(Out_2[0]));
  nm_d_gated nm_d_gated_2 (.D(D[1]), .E(set), .Q(Out[1]), .Q_2(Out_2[1]));
  nm_d_gated nm_d_gated_3 (.D(D[2]), .E(set), .Q(Out[2]), .Q_2(Out_2[2]));
  nm_d_gated nm_d_gated_4 (.D(D[3]), .E(set), .Q(Out[3]), .Q_2(Out_2[3]));
  nm_d_gated nm_d_gated_5 (.D(D[4]), .E(set), .Q(Out[4]), .Q_2(Out_2[4]));
  nm_d_gated nm_d_gated_6 (.D(D[5]), .E(set), .Q(Out[5]), .Q_2(Out_2[5]));
  nm_d_gated nm_d_gated_7 (.D(D[6]), .E(set), .Q(Out[6]), .Q_2(Out_2[6]));
  nm_d_gated nm_d_gated_8 (.D(D[7]), .E(set), .Q(Out[7]), .Q_2(Out_2[7]));
endmodule
