// Digital circuit nm_conditionals_min.dig as structural Verilog
module nm_conditionals_min (
  input  [7:0] In,
  output gtz,
  output ltz,
  output eqz
);

  nm_nor8 nm_nor8_1 (
    .Out(eqz), .In_1(In[0]), .In_2(In[1]), .In_3(In[2]), .In_4(In[3]), .In_5(In[4]), .In_6(In[5]),
    .In_7(In[6]), .In_8(In[7]));
  nm_nor nm_nor_1 (.In_1(eqz), .In_2(In[7]), .Out(gtz));

  assign ltz = In[7];
endmodule
