// Digital circuit nm_conditionals_prestage.dig as structural Verilog
module nm_conditionals_prestage (
  input  [7:0] In,
  output zr,
  output ng
);

  nm_nor8 nm_nor8_1 (
    .Out(zr), .In_1(In[0]), .In_2(In[1]), .In_3(In[2]), .In_4(In[3]), .In_5(In[4]), .In_6(In[5]),
    .In_7(In[6]), .In_8(In[7]));

  assign ng = In[7];
endmodule
