// Digital circuit nm_counter16_resetn.dig as structural Verilog
module nm_counter16_resetn (
  input  [15:0] D,
  input  clk,
  input  set,
  input  reset,
  output [15:0] Out,
  output ovf
);

  wire notconnected_1_out;
  wire [15:0] nm_adder16_1_sum, nm_mux16_1_out;

  // NotConnected on notconnected_1_out
  nm_adder16 nm_adder16_1 (.A(Out), .B(16'h1), .c_in(notconnected_1_out), .sum(nm_adder16_1_sum), .c_out(ovf));
  nm_mux16 nm_mux16_1 (.A(nm_adder16_1_sum), .s(set), .B(D), .Out(nm_mux16_1_out));
  nm_byte2_resetn nm_byte2_resetn_1 (.D(nm_mux16_1_out), .clk(clk), .reset(reset), .Out(Out));  // open: Out_2
endmodule
