// Digital circuit nm_counter8.dig as structural Verilog
module nm_counter8 (
  input  [7:0] D,
  input  clk,
  input  load,
  output [7:0] Out
);

  wire nm_tff_d_1_q_2, nm_tff_d_2_q_2, nm_tff_d_3_q_2, nm_tff_d_4_q_2, nm_tff_d_5_q_2, nm_tff_d_6_q_2,
       nm_tff_d_7_q_2;

  nm_tff_d nm_tff_d_1 (.T(clk), .D_load(load), .D(D[0]), .Q(Out[0]), .Q_2(nm_tff_d_1_q_2));
  nm_tff_d nm_tff_d_2 (.T(nm_tff_d_1_q_2), .D_load(load), .D(D[1]), .Q(Out[1]), .Q_2(nm_tff_d_2_q_2));
  nm_tff_d nm_tff_d_3 (.T(nm_tff_d_2_q_2), .D_load(load), .D(D[2]), .Q(Out[2]), .Q_2(nm_tff_d_3_q_2));
  nm_tff_d nm_tff_d_4 (.T(nm_tff_d_3_q_2), .D_load(load), .D(D[3]), .Q(Out[3]), .Q_2(nm_tff_d_4_q_2));
  nm_tff_d nm_tff_d_5 (.T(nm_tff_d_4_q_2), .D_load(load), .D(D[4]), .Q(Out[4]), .Q_2(nm_tff_d_5_q_2));
  nm_tff_d nm_tff_d_6 (.T(nm_tff_d_5_q_2), .D_load(load), .D(D[5]), .Q(Out[5]), .Q_2(nm_tff_d_6_q_2));
  nm_tff_d nm_tff_d_7 (.T(nm_tff_d_6_q_2), .D_load(load), .D(D[6]), .Q(Out[6]), .Q_2(nm_tff_d_7_q_2));
  nm_tff_d nm_tff_d_8 (.T(nm_tff_d_7_q_2), .D_load(load), .D(D[7]), .Q(Out[7]));  // open: Q_2
endmodule
