// Digital circuit nm_counter8_resetn.dig as structural Verilog
module nm_counter8_resetn (
  input  clk,
  input  r,
  output [7:0] Out
);

  wire nm_tff_resetn_1_q_2, nm_tff_resetn_2_q_2, nm_tff_resetn_3_q_2, nm_tff_resetn_4_q_2,
       nm_tff_resetn_5_q_2, nm_tff_resetn_6_q_2, nm_tff_resetn_7_q_2;

  nm_tff_resetn nm_tff_resetn_1 (.T(clk), .Q(Out[0]), .Q_2(nm_tff_resetn_1_q_2), .r(r));
  nm_tff_resetn nm_tff_resetn_2 (.T(nm_tff_resetn_1_q_2), .Q(Out[1]), .Q_2(nm_tff_resetn_2_q_2), .r(r));
  nm_tff_resetn nm_tff_resetn_3 (.T(nm_tff_resetn_2_q_2), .Q(Out[2]), .Q_2(nm_tff_resetn_3_q_2), .r(r));
  nm_tff_resetn nm_tff_resetn_4 (.T(nm_tff_resetn_3_q_2), .Q(Out[3]), .Q_2(nm_tff_resetn_4_q_2), .r(r));
  nm_tff_resetn nm_tff_resetn_5 (.T(nm_tff_resetn_4_q_2), .Q(Out[4]), .Q_2(nm_tff_resetn_5_q_2), .r(r));
  nm_tff_resetn nm_tff_resetn_6 (.T(nm_tff_resetn_5_q_2), .Q(Out[5]), .Q_2(nm_tff_resetn_6_q_2), .r(r));
  nm_tff_resetn nm_tff_resetn_7 (.T(nm_tff_resetn_6_q_2), .Q(Out[6]), .Q_2(nm_tff_resetn_7_q_2), .r(r));
  nm_tff_resetn nm_tff_resetn_8 (.T(nm_tff_resetn_7_q_2), .Q(Out[7]), .r(r));  // open: Q_2
endmodule
