// Digital circuit nm_counter8_sync.dig as structural Verilog
module nm_counter8_sync (
  input  [7:0] D,
  input  clk,
  input  load,
  output [7:0] Out
);

  wire nm_and_1_out, nm_and_2_out, nm_and_3_out, nm_and_4_out, nm_and_5_out, nm_and_6_out;

  nm_tff_clk_d nm_tff_clk_d_1 (.T(1'b1), .D_load(load), .D(D[0]), .clk(clk), .Q(Out[0]));  // open: Q_2
  nm_tff_clk_d nm_tff_clk_d_2 (.T(Out[0]), .D_load(load), .D(D[1]), .clk(clk), .Q(Out[1]));  // open: Q_2
  nm_and nm_and_1 (.In_1(Out[0]), .In_2(Out[1]), .Out(nm_and_1_out));
  nm_tff_clk_d nm_tff_clk_d_3 (.T(nm_and_1_out), .D_load(load), .D(D[2]), .clk(clk), .Q(Out[2]));  // open: Q_2
  nm_and nm_and_2 (.In_1(nm_and_1_out), .In_2(Out[2]), .Out(nm_and_2_out));
  nm_tff_clk_d nm_tff_clk_d_4 (.T(nm_and_2_out), .D_load(load), .D(D[3]), .clk(clk), .Q(Out[3]));  // open: Q_2
  nm_and nm_and_3 (.In_1(nm_and_2_out), .In_2(Out[3]), .Out(nm_and_3_out));
  nm_tff_clk_d nm_tff_clk_d_5 (.T(nm_and_3_out), .D_load(load), .D(D[4]), .clk(clk), .Q(Out[4]));  // open: Q_2
  nm_and nm_and_4 (.In_1(nm_and_3_out), .In_2(Out[4]), .Out(nm_and_4_out));
  nm_tff_clk_d nm_tff_clk_d_6 (.T(nm_and_4_out), .D_load(load), .D(D[5]), .clk(clk), .Q(Out[5]));  // open: Q_2
  nm_and nm_and_5 (.In_1(nm_and_4_out), .In_2(Out[5]), .Out(nm_and_5_out));
  nm_tff_clk_d nm_tff_clk_d_7 (.T(nm_and_5_out), .D_load(load), .D(D[6]), .clk(clk), .Q(Out[6]));  // open: Q_2
  nm_and nm_and_6 (.In_1(nm_and_5_out), .In_2(Out[6]), .Out(nm_and_6_out));
  nm_tff_clk_d nm_tff_clk_d_8 (.T(nm_and_6_out), .D_load(load), .D(D[7]), .clk(clk), .Q(Out[7]));  // open: Q_2
endmodule
