// Digital circuit nm_decoder2x4.dig as structural Verilog
module nm_decoder2x4 (
  input  [1:0] In,
  output A,
  output B,
  output C,
  output D
);

  wire nm_not_1_out, nm_not_2_out;

  nm_Not nm_not_1 (.In(In[0]), .Out(nm_not_1_out));
  nm_Not nm_not_2 (.In(In[1]), .Out(nm_not_2_out));
  nm_And nm_and_1 (.In_1(nm_not_1_out), .In_2(nm_not_2_out), .Out(A));
  nm_And nm_and_2 (.In_1(In[0]), .In_2(nm_not_2_out), .Out(B));
  nm_And nm_and_3 (.In_1(nm_not_1_out), .In_2(In[1]), .Out(C));
  nm_And nm_and_4 (.In_1(In[0]), .In_2(In[1]), .Out(D));
endmodule
