// Digital circuit nm_dff.dig as structural Verilog
module nm_dff (
  input  D,
  input  clk,
  input  r,
  output Q,
  output Q_2
);

  wire delay_1_out, nm_not_1_out;

  Delay delay_1 (.in(clk), .out(delay_1_out));
  nm_not nm_not_1 (.In(r), .Out(nm_not_1_out));
  nm_dff_resetn nm_dff_resetn_1 (.D(D), .clk(delay_1_out), .r(nm_not_1_out), .Q(Q), .Q_2(Q_2));
endmodule
