// Digital circuit nm_dff_async.dig as structural Verilog
module nm_dff_async (
  input  D,
  input  clk,
  input  r,
  input  s,
  output Q,
  output Q_2
);

  wire delay_1_out, nm_not_1_out, nm_not_2_out;

  Delay delay_1 (.in(D), .out(delay_1_out));
  nm_not nm_not_1 (.In(s), .Out(nm_not_1_out));
  nm_not nm_not_2 (.In(r), .Out(nm_not_2_out));
  nm_dff_asyncn nm_dff_asyncn_1 (.D(delay_1_out), .clk(clk), .r(nm_not_2_out), .s(nm_not_1_out), .Q(Q), .Q_2(Q_2));
endmodule
