// Digital circuit nm_dff_asyncn.dig as structural Verilog
module nm_dff_asyncn (
  input  D,
  input  clk,
  input  r,
  input  s,
  output Q,
  output Q_2
);

  wire nm_nand3_1_out, nm_nand3_2_out, nm_nand3_3_out, nm_nand3_4_out;

  nm_nand3 nm_nand3_1 (.In_1(s), .In_2(nm_nand3_4_out), .In_3(nm_nand3_2_out), .Out(nm_nand3_1_out));
  nm_nand3 nm_nand3_2 (.In_1(nm_nand3_1_out), .In_2(clk), .In_3(r), .Out(nm_nand3_2_out));
  nm_nand3 nm_nand3_3 (.In_1(nm_nand3_2_out), .In_2(clk), .In_3(nm_nand3_4_out), .Out(nm_nand3_3_out));
  nm_nand3 nm_nand3_4 (.In_1(nm_nand3_3_out), .In_2(D), .In_3(r), .Out(nm_nand3_4_out));
  nm_nand3 nm_nand3_5 (.In_1(s), .In_2(nm_nand3_2_out), .In_3(Q_2), .Out(Q));
  nm_nand3 nm_nand3_6 (.In_1(Q), .In_2(nm_nand3_3_out), .In_3(r), .Out(Q_2));
endmodule
