// Digital circuit nm_dff_noset.dig as structural Verilog
module nm_dff_noset (
  input  D,
  input  clk,
  output Q,
  output Q_2
);

  wire nm_sr2_1_1_q, nm_sr2_1_1_q_2, nm_sr_1_q_2;

  nm_sr nm_sr_1 (.s(nm_sr2_1_1_q_2), .r(clk), .Q_2(nm_sr_1_q_2));  // open: Q
  nm_sr2_1 nm_sr2_1_1 (.s__1(nm_sr_1_q_2), .s__2(clk), .r(D), .Q(nm_sr2_1_1_q), .Q_2(nm_sr2_1_1_q_2));
  nm_sr nm_sr_2 (.s(nm_sr_1_q_2), .r(nm_sr2_1_1_q), .Q(Q), .Q_2(Q_2));
endmodule
