// Digital circuit nm_dff_resetn.dig as structural Verilog
module nm_dff_resetn (
  input  D,
  input  clk,
  input  r,
  output Q,
  output Q_2
);

  wire nm_nand3_1_out, nm_nand3_2_out, nm_nand3_3_out, nm_nand_1_out;

  nm_nand nm_nand_1 (.In_1(nm_nand3_3_out), .In_2(nm_nand3_1_out), .Out(nm_nand_1_out));
  nm_nand3 nm_nand3_1 (.In_1(nm_nand_1_out), .In_2(clk), .In_3(r), .Out(nm_nand3_1_out));
  nm_nand3 nm_nand3_2 (.In_1(nm_nand3_1_out), .In_2(clk), .In_3(nm_nand3_3_out), .Out(nm_nand3_2_out));
  nm_nand3 nm_nand3_3 (.In_1(nm_nand3_2_out), .In_2(D), .In_3(r), .Out(nm_nand3_3_out));
  nm_nand nm_nand_2 (.In_1(nm_nand3_1_out), .In_2(Q_2), .Out(Q));
  nm_nand3 nm_nand3_4 (.In_1(Q), .In_2(nm_nand3_2_out), .In_3(r), .Out(Q_2));
endmodule
