// Digital circuit nm_dmux.dig as structural Verilog
module nm_dmux (
  input  In,
  input  sel,
  output Out_1,
  output Out_2
);

  wire nm_not_1_out;

  nm_Not nm_not_1 (.In(sel), .Out(nm_not_1_out));
  nm_And nm_and_1 (.In_1(In), .In_2(nm_not_1_out), .Out(Out_1));
  nm_And nm_and_2 (.In_1(In), .In_2(sel), .Out(Out_2));
endmodule
