// Digital circuit nm_dmuxn.dig as structural Verilog
module nm_dmuxn (
  input  In,
  input  sel,
  output Out_1,
  output Out_2
);

  wire nm_not_1_out;

  nm_not nm_not_1 (.In(sel), .Out(nm_not_1_out));
  nm_nor nm_nor_1 (.In_1(In), .In_2(sel), .Out(Out_1));
  nm_nor nm_nor_2 (.In_1(In), .In_2(nm_not_1_out), .Out(Out_2));
endmodule
