// Digital circuit nm_enable.dig as structural Verilog
module nm_enable (
  input  In,
  input  en,
  output Out
);

  wire nm_and_1_out, nm_and_2_out, nm_not_1_out, nm_not_2_out, nm_xor_1_out;

  nm_Not nm_not_1 (.In(In), .Out(nm_not_1_out));
  nm_Not nm_not_2 (.In(en), .Out(nm_not_2_out));
  nm_And nm_and_1 (.In_1(nm_not_1_out), .In_2(en), .Out(nm_and_1_out));
  nm_Xor nm_xor_1 (.In_1(nm_not_2_out), .In_2(nm_and_1_out), .Out(nm_xor_1_out));
  nm_And nm_and_2 (.In_1(nm_and_1_out), .In_2(en), .Out(nm_and_2_out));
  PFET pfet_1 (.G(nm_xor_1_out), .S(1'b1), .D(Out));
  NFET nfet_1 (.G(nm_and_2_out), .D(Out), .S(1'b0));
endmodule

/* Test case:
en In Out

0 0 Z
0 1 Z
1 0 0
1 1 1
*/
