// Digital circuit nm_enableocn8.dig as structural Verilog
module nm_enableocn8 (
  input  [7:0] In,
  input  en,
  output [7:0] Out
);

  wire nfet_1_s;

  NFET nfet_1 (.G(In[0]), .D(Out[0]), .S(nfet_1_s));
  NFET nfet_2 (.G(In[1]), .D(Out[1]), .S(nfet_1_s));
  NFET nfet_3 (.G(en), .D(nfet_1_s), .S(1'b0));
  NFET nfet_4 (.G(In[2]), .D(Out[2]), .S(nfet_1_s));
  NFET nfet_5 (.G(In[3]), .D(Out[3]), .S(nfet_1_s));
  NFET nfet_6 (.G(In[4]), .D(Out[4]), .S(nfet_1_s));
  NFET nfet_7 (.G(In[5]), .D(Out[5]), .S(nfet_1_s));
  NFET nfet_8 (.G(In[6]), .D(Out[6]), .S(nfet_1_s));
  NFET nfet_9 (.G(In[7]), .D(Out[7]), .S(nfet_1_s));
endmodule
