// Digital circuit nm_halfadder+.dig as structural Verilog
module nm_halfadder (
  input  A,
  input  B,
  output sum,
  output carry,
  output \nand ,
  output \nor 
);

  nm_xor nm_xor_1 (.Out(sum), .In_1(A), .In_2(B), .\nor (\nor ));
  nm_and nm_and_1 (.Out(carry), .In_1(A), .In_2(B), .Out_2(\nand ));
endmodule
