// Digital circuit nm_jk.dig as structural Verilog
module nm_jk (
  input  J,
  input  clk,
  input  K,
  input  r,
  output Q,
  output Q_2
);

  wire nm_not_1_out;

  nm_not nm_not_1 (.In(r), .Out(nm_not_1_out));
  nm_jk_resetn nm_jk_resetn_1 (.J(J), .clk(clk), .r(nm_not_1_out), .K(K), .Q(Q), .Q_2(Q_2));
endmodule
