// Digital circuit nm_jk_async.dig as structural Verilog
module nm_jk_async (
  input  J,
  input  clk,
  input  r,
  input  s,
  input  K,
  output Q,
  output Q_2
);

  wire nm_not_1_out, nm_not_2_out;

  nm_not nm_not_1 (.In(r), .Out(nm_not_1_out));
  nm_not nm_not_2 (.In(s), .Out(nm_not_2_out));
  nm_jk_asyncn nm_jk_asyncn_1 (.J(J), .clk(clk), .r(nm_not_1_out), .s(nm_not_2_out), .K(K), .Q(Q), .Q_2(Q_2));
endmodule
