// Digital circuit nm_jk_asyncn.dig as structural Verilog
module nm_jk_asyncn (
  input  J,
  input  clk,
  input  r,
  input  s,
  input  K,
  output Q,
  output Q_2
);

  wire nm_nand3_1_out, nm_nand3_2_out;

  nm_nand3 nm_nand3_1 (.In_1(Q_2), .In_2(J), .In_3(clk), .Out(nm_nand3_1_out));
  nm_nand3 nm_nand3_2 (.In_1(clk), .In_2(K), .In_3(Q), .Out(nm_nand3_2_out));
  nm_nand3 nm_nand3_3 (.In_1(s), .In_2(nm_nand3_1_out), .In_3(Q_2), .Out(Q));
  nm_nand3 nm_nand3_4 (.In_1(Q), .In_2(nm_nand3_2_out), .In_3(r), .Out(Q_2));
endmodule
