// Digital circuit nm_jk_resetn.dig as structural Verilog
module nm_jk_resetn (
  input  J,
  input  clk,
  input  r,
  input  K,
  output Q,
  output Q_2
);

  wire nm_nand3_1_out, nm_nand3_2_out;

  nm_nand3 nm_nand3_1 (.In_1(Q_2), .In_2(J), .In_3(clk), .Out(nm_nand3_1_out));
  nm_nand3 nm_nand3_2 (.In_1(clk), .In_2(K), .In_3(Q), .Out(nm_nand3_2_out));
  nm_nand nm_nand_1 (.In_1(nm_nand3_1_out), .In_2(Q_2), .Out(Q));
  nm_nand3 nm_nand3_3 (.In_1(Q), .In_2(nm_nand3_2_out), .In_3(r), .Out(Q_2));
endmodule
