// Digital circuit nm_mux.dig as structural Verilog
module nm_mux (
  input  In_1,
  input  sel,
  input  In_2,
  output Out
);

  wire nm_aoi2_2_1_out, nm_not_1_out;

  nm_Not nm_not_1 (.In(sel), .Out(nm_not_1_out));
  nm_AOI2_2 nm_aoi2_2_1 (.In_1(In_1), .In_2(nm_not_1_out), .In_3(In_2), .In_4(sel), .Out(nm_aoi2_2_1_out));
  nm_Not nm_not_2 (.In(nm_aoi2_2_1_out), .Out(Out));
endmodule
