// Digital circuit nm_mux2x4.dig as structural Verilog
module nm_mux2x4 (
  input  A,
  input  [1:0] s,
  input  B,
  input  C,
  input  D,
  output Out
);

  wire nm_aoi2_2_4_1_out, nm_decoder_2x4_1_p1, nm_decoder_2x4_1_p3, nm_decoder_2x4_1_p4, nm_decoder_2x4_1_p5;

  // nm_decoder_2x4 nm_decoder_2x4_1: pin names not known; wires that end beside it: nm_decoder_2x4_1_p1, s, nm_decoder_2x4_1_p3, nm_decoder_2x4_1_p4, nm_decoder_2x4_1_p5
  nm_AOI2_2_4 nm_aoi2_2_4_1 (
    .In_1(A), .In_2(nm_decoder_2x4_1_p1), .In_3(B), .In_4(nm_decoder_2x4_1_p3), .In_5(C),
    .In_6(nm_decoder_2x4_1_p4), .In_7(D), .In_8(nm_decoder_2x4_1_p5), .Out(nm_aoi2_2_4_1_out));
  nm_Not nm_not_1 (.In(nm_aoi2_2_4_1_out), .Out(Out));
endmodule
