// Digital circuit nm_mux8.dig as structural Verilog
module nm_mux8 (
  input  [7:0] A,
  input  s,
  input  [7:0] B,
  output [7:0] Out
);

  nm_mux nm_mux_1 (.In_1(A[0]), .s(s), .In_2(B[0]), .Out(Out[0]));
  nm_mux nm_mux_2 (.In_1(A[1]), .s(s), .In_2(B[1]), .Out(Out[1]));
  nm_mux nm_mux_3 (.In_1(A[2]), .s(s), .In_2(B[2]), .Out(Out[2]));
  nm_mux nm_mux_4 (.In_1(A[3]), .s(s), .In_2(B[3]), .Out(Out[3]));
  nm_mux nm_mux_5 (.In_1(A[4]), .s(s), .In_2(B[4]), .Out(Out[4]));
  nm_mux nm_mux_6 (.In_1(A[5]), .s(s), .In_2(B[5]), .Out(Out[5]));
  nm_mux nm_mux_7 (.In_1(A[6]), .s(s), .In_2(B[6]), .Out(Out[6]));
  nm_mux nm_mux_8 (.In_1(A[7]), .s(s), .In_2(B[7]), .Out(Out[7]));
endmodule
