// Digital circuit nm_muxn.dig as structural Verilog
module nm_muxn (
  input  In_1,
  input  sel,
  input  In_2,
  output Out
);

  wire nm_not_1_out;

  nm_not nm_not_1 (.In(sel), .Out(nm_not_1_out));
  nm_aoi2_2 nm_aoi2_2_1 (.In_1(In_1), .In_2(nm_not_1_out), .In_3(In_2), .In_4(sel), .Out(Out));
endmodule
