// Digital circuit nm_muxn16.dig as structural Verilog
module nm_muxn16 (
  input  [15:0] A,
  input  s,
  input  [15:0] B,
  output [15:0] Out
);

  nm_muxn8 nm_muxn8_1 (.A(A[7:0]), .s(s), .B(B[7:0]), .Out(Out[7:0]));
  nm_muxn8 nm_muxn8_2 (.A(A[15:8]), .s(s), .B(B[15:8]), .Out(Out[15:8]));
endmodule
