// Digital circuit nm_muxn8.dig as structural Verilog
module nm_muxn8 (
  input  [7:0] A,
  input  s,
  input  [7:0] B,
  output [7:0] Out
);

  wire nm_not_1_out;

  nm_not nm_not_1 (.In(s), .Out(nm_not_1_out));
  nm_aoi2_2 nm_aoi2_2_1 (.In_1(A[0]), .In_2(nm_not_1_out), .In_3(B[0]), .In_4(s), .Out(Out[0]));
  nm_aoi2_2 nm_aoi2_2_2 (.In_1(A[1]), .In_2(nm_not_1_out), .In_3(B[1]), .In_4(s), .Out(Out[1]));
  nm_aoi2_2 nm_aoi2_2_3 (.In_1(A[2]), .In_2(nm_not_1_out), .In_3(B[2]), .In_4(s), .Out(Out[2]));
  nm_aoi2_2 nm_aoi2_2_4 (.In_1(A[3]), .In_2(nm_not_1_out), .In_3(B[3]), .In_4(s), .Out(Out[3]));
  nm_aoi2_2 nm_aoi2_2_5 (.In_1(A[4]), .In_2(nm_not_1_out), .In_3(B[4]), .In_4(s), .Out(Out[4]));
  nm_aoi2_2 nm_aoi2_2_6 (.In_1(A[5]), .In_2(nm_not_1_out), .In_3(B[5]), .In_4(s), .Out(Out[5]));
  nm_aoi2_2 nm_aoi2_2_7 (.In_1(A[6]), .In_2(nm_not_1_out), .In_3(B[6]), .In_4(s), .Out(Out[6]));
  nm_aoi2_2 nm_aoi2_2_8 (.In_1(A[7]), .In_2(nm_not_1_out), .In_3(B[7]), .In_4(s), .Out(Out[7]));
endmodule
