// Digital circuit nm_nand2x1.dig as structural Verilog
module nm_nand2x1 (
  input  In_1,
  input  In_2,
  input  In_all,
  output Out
);

  wire nfet_1_s;

  NFET nfet_1 (.G(In_1), .D(Out), .S(nfet_1_s));
  NFET nfet_2 (.G(In_all), .D(nfet_1_s), .S(1'b0));
  PullUp pullup_1 (.out(Out));
  NFET nfet_3 (.G(In_2), .D(Out), .S(nfet_1_s));
endmodule
