// Digital circuit nm_nand3.dig as structural Verilog
module nm_nand3 (
  input  In_1,
  input  In_2,
  input  In_3,
  output Out
);

  wire nfet_1_s, nfet_2_s;

  NFET nfet_1 (.G(In_1), .D(Out), .S(nfet_1_s));
  NFET nfet_2 (.G(In_2), .D(nfet_1_s), .S(nfet_2_s));
  NFET nfet_3 (.G(In_3), .D(nfet_2_s), .S(1'b0));
  PullUp pullup_1 (.out(Out));
endmodule
