// Digital circuit nm_nor3.dig as structural Verilog
module nm_nor3 (
  input  In_1,
  input  In_2,
  input  In_3,
  output Out
);

  NFET nfet_1 (.G(In_1), .D(Out), .S(1'b0));
  PullUp pullup_1 (.out(Out));
  NFET nfet_2 (.G(In_2), .D(Out), .S(1'b0));
  NFET nfet_3 (.G(In_3), .D(Out), .S(1'b0));
endmodule
