// Digital circuit nm_opflag_decoder_FET80.dig as structural Verilog
module nm_opflag_decoder_FET80 (
  input  X_plus_Y,
  input  X_Y,
  input  Y_X,
  input  Y_X_2,
  input  Y_X_3,
  output nx,
  output ny,
  output f,
  output no
);

  nm_nor3 nm_nor3_1 (.In_1(X_plus_Y), .In_2(Y_X), .In_3(Y_X_2), .Out(nx));
  nm_nor3 nm_nor3_2 (.In_1(X_plus_Y), .In_2(X_Y), .In_3(Y_X_2), .Out(ny));
  nm_nor nm_nor_1 (.In_1(Y_X_2), .In_2(Y_X_3), .Out(f));
  nm_nor nm_nor_2 (.In_1(X_plus_Y), .In_2(Y_X_2), .Out(no));
endmodule
