// Digital circuit nm_or8.dig as structural Verilog
module nm_or8 (
  input  In_1,
  input  In_2,
  input  In_3,
  input  In_4,
  input  In_5,
  input  In_6,
  input  In_7,
  input  In_8,
  output Out
);

  wire nm_nor8_1_out;

  nm_nor8 nm_nor8_1 (
    .In_1(In_1), .In_2(In_2), .In_3(In_3), .In_4(In_4), .In_5(In_5), .In_6(In_6), .In_7(In_7), .In_8(In_8),
    .Out(nm_nor8_1_out));
  nm_not nm_not_1 (.In(nm_nor8_1_out), .Out(Out));
endmodule
