// Digital circuit nm_reg16_resetn.dig as structural Verilog
module nm_reg16_resetn (
  input  [15:0] D,
  input  clk,
  input  reset,
  input  en,
  output [15:0] Out,
  output [15:0] V
);

  nm_reg8_resetn nm_reg8_resetn_1 (.D(D[7:0]), .clk(clk), .reset(reset), .en(en), .Out(Out[7:0]), .V(V[7:0]));
  nm_reg8_resetn nm_reg8_resetn_2 (.D(D[15:8]), .clk(clk), .reset(reset), .en(en), .Out(Out[15:8]), .V(V[15:8]));
endmodule
