// Digital circuit nm_regoc8_resetn.dig as structural Verilog
module nm_regoc8_resetn (
  input  [7:0] D,
  input  clk,
  input  reset,
  input  en,
  output [7:0] Out,
  output [7:0] V
);

  nm_bitoc_resetn nm_bitoc_resetn_1 (.D(D[0]), .clk(clk), .reset(reset), .en(en), .Out(Out[0]), .V(V[0]));
  nm_bitoc_resetn nm_bitoc_resetn_2 (.D(D[1]), .clk(clk), .reset(reset), .en(en), .Out(Out[1]), .V(V[1]));
  nm_bitoc_resetn nm_bitoc_resetn_3 (.D(D[2]), .clk(clk), .reset(reset), .en(en), .Out(Out[2]), .V(V[2]));
  nm_bitoc_resetn nm_bitoc_resetn_4 (.D(D[3]), .clk(clk), .reset(reset), .en(en), .Out(Out[3]), .V(V[3]));
  nm_bitoc_resetn nm_bitoc_resetn_5 (.D(D[4]), .clk(clk), .reset(reset), .en(en), .Out(Out[4]), .V(V[4]));
  nm_bitoc_resetn nm_bitoc_resetn_6 (.D(D[5]), .clk(clk), .reset(reset), .en(en), .Out(Out[5]), .V(V[5]));
  nm_bitoc_resetn nm_bitoc_resetn_7 (.D(D[6]), .clk(clk), .reset(reset), .en(en), .Out(Out[6]), .V(V[6]));
  nm_bitoc_resetn nm_bitoc_resetn_8 (.D(D[7]), .clk(clk), .reset(reset), .en(en), .Out(Out[7]), .V(V[7]));
endmodule
