// Digital circuit nm_rs.dig as structural Verilog
module nm_rs (
  input  s,
  input  r,
  output Q,
  output Q_2
);

  nm_nor nm_nor_1 (.In_1(r), .In_2(Q_2), .Out(Q));
  nm_nor nm_nor_2 (.In_1(Q), .In_2(s), .Out(Q_2));
endmodule
