// Digital circuit nm_sr1-2.dig as structural Verilog
module nm_sr1_2 (
  input  s,
  input  r__1,
  input  r__2,
  output Q,
  output Q_2
);

  nm_nand nm_nand_1 (.In_1(s), .In_2(Q_2), .Out(Q));
  nm_nand3 nm_nand3_1 (.In_1(Q), .In_2(r__1), .In_3(r__2), .Out(Q_2));
endmodule
