// Digital circuit nm_sr2-1.dig as structural Verilog
module nm_sr2_1 (
  input  s__1,
  input  r,
  input  s__2,
  output Q,
  output Q_2
);

  nm_nand3 nm_nand3_1 (.In_1(s__1), .In_2(s__2), .In_3(Q_2), .Out(Q));
  nm_nand nm_nand_1 (.In_1(Q), .In_2(r), .Out(Q_2));
endmodule
