// Digital circuit nm_sr2-2.dig as structural Verilog
module nm_sr2_2 (
  input  s__1,
  input  r__1,
  input  r__2,
  input  s__2,
  output Q,
  output Q_2
);

  nm_nand3 nm_nand3_1 (.In_1(s__1), .In_2(s__2), .In_3(Q_2), .Out(Q));
  nm_nand3 nm_nand3_2 (.In_1(Q), .In_2(r__1), .In_3(r__2), .Out(Q_2));
endmodule
