// Digital circuit nm_srn.dig as structural Verilog
module nm_srn (
  input  s,
  input  r,
  output Q,
  output Q_2
);

  nm_nand nm_nand_1 (.In_1(s), .In_2(Q_2), .Out(Q));
  nm_nand nm_nand_2 (.In_1(Q), .In_2(r), .Out(Q_2));
endmodule
