// Digital circuit nm_startup.dig as structural Verilog
module nm_startup (
  input  r,
  input  clk_e,
  input  clk_s,
  output zero_bus,
  output set_master
);

  wire nm_nand_1_out, nm_tff_resetn_1_q_2;

  nm_nand nm_nand_1 (.In_1(nm_tff_resetn_1_q_2), .In_2(clk_e), .Out(nm_nand_1_out));
  nm_tff_resetn nm_tff_resetn_1 (.T(nm_nand_1_out), .Q_2(nm_tff_resetn_1_q_2), .r(r));  // open: Q
  nm_and nm_and_1 (.In_1(clk_e), .In_2(nm_tff_resetn_1_q_2), .Out(zero_bus));
  nm_and nm_and_2 (.In_1(clk_s), .In_2(nm_tff_resetn_1_q_2), .Out(set_master));
endmodule
