// Digital circuit nm_tff_asyncn.dig as structural Verilog
module nm_tff_asyncn (
  input  T,
  input  clk,
  input  r,
  input  s,
  output Q,
  output Q_2
);

  nm_jk_asyncn nm_jk_asyncn_1 (.J(T), .clk(clk), .K(T), .Q(Q), .Q_2(Q_2), .r(r), .s(s));
endmodule
