// Digital circuit nm_tff_d_notd.dig as structural Verilog
module nm_tff_d_notd (
  input  T,
  input  D_load,
  input  D,
  input  D_2,
  output Q,
  output Q_2
);

  wire nm_nand_1_out, nm_nand_2_out;

  nm_nand nm_nand_1 (.In_1(D), .In_2(D_load), .Out(nm_nand_1_out));
  nm_tff_asyncn nm_tff_asyncn_1 (.T(T), .Q(Q), .Q_2(Q_2), .r(nm_nand_2_out), .s(nm_nand_1_out));
  nm_nand nm_nand_2 (.In_1(D_load), .In_2(D_2), .Out(nm_nand_2_out));
endmodule
