// Digital circuit nm_zero8.dig as structural Verilog
module nm_zero8 (
  input  [7:0] In,
  input  zr,
  output [7:0] Out
);

  wire nm_not_1_out;

  nm_Not nm_not_1 (.In(zr), .Out(nm_not_1_out));
  nm_And8x1 nm_and8x1_1 (.In_1(In), .In_2(nm_not_1_out), .Out(Out));
endmodule
