// Digital circuit nm_zerooc8.dig as structural Verilog
module nm_zerooc8 (
  input  [7:0] Bus,
  input  zero
);

  NFET nfet_1 (.G(zero), .D(Bus[0]), .S(1'b0));
  NFET nfet_2 (.G(zero), .D(Bus[1]), .S(1'b0));
  NFET nfet_3 (.G(zero), .D(Bus[2]), .S(1'b0));
  NFET nfet_4 (.G(zero), .D(Bus[3]), .S(1'b0));
  NFET nfet_5 (.G(zero), .D(Bus[4]), .S(1'b0));
  NFET nfet_6 (.G(zero), .D(Bus[5]), .S(1'b0));
  NFET nfet_7 (.G(zero), .D(Bus[6]), .S(1'b0));
  NFET nfet_8 (.G(zero), .D(Bus[7]), .S(1'b0));
endmodule
