// Digital circuit s2.dig as structural Verilog
module s2 (
  input  _1,
  input  _2,
  input  D,
  input  S
);

  wire nfet_1_s;

  NFET nfet_1 (.G(_1), .D(D), .S(nfet_1_s));
  NFET nfet_2 (.G(_2), .D(nfet_1_s), .S(S));
endmodule
