// Digital circuit tff_asyncn.dig as structural Verilog
module tff_asyncn (
  input  T,
  input  clk,
  input  r,
  input  s,
  output Q,
  output Q_2
);

  JK_FF_AS jk_ff_as_1 (.Set(~s), .J(T), .C(clk), .K(T), .Clr(~r), .Q(Q), .nQ(Q_2));
endmodule
