// Digital circuit toy.dig as structural Verilog
module toy (
  input  Reset,
  input  Set_D,
  input  Save_ACC,
  input  Load_ACC,
  input  Set_A,
  input  Load_A,
  input  In_0,
  input  In_1,
  input  In_2,
  input  In_3,
  input  In_4,
  input  In_5,
  input  In_6,
  input  In_7,
  input  Load_In,
  input  in_22,
  input  in_23,
  input  in_24,
  input  in_25,
  input  in_26,
  input  in_27,
  input  Load_M,
  input  Set_M,
  output [7:0] ALU,
  output [7:0] D,
  output [7:0] ACC,
  output [7:0] A,
  output [7:0] In,
  output [7:0] Bus,
  output [7:0] M
);

  wire nm_alu_hack8_1_ng, nm_alu_hack8_1_zr;

  nm_enable8 nm_enable8_1 (.In({In_7, In_6, In_5, In_4, In_3, In_2, In_1, In_0}), .en(Load_In), .Out(Bus));
  nm_byte nm_byte_1 (.D(Bus), .clk(Set_D), .reset(Reset), .Out(D));
  nm_ALU_HACK8 nm_alu_hack8_1 (
    .X(D), .Y(Bus), .Out(ALU), .zr(nm_alu_hack8_1_zr), .ng(nm_alu_hack8_1_ng), .zx(in_27), .nx(in_22),
    .zy(in_23), .ny(in_24), .f(in_25), .no(in_26));
  LED Zero (.in(nm_alu_hack8_1_zr));
  LED Negative (.in(nm_alu_hack8_1_ng));
  nm_Reg8 nm_reg8_1 (.D(ALU), .clk(Save_ACC), .reset(Reset), .en(Load_ACC), .Out(Bus), .V(ACC));
  nm_Reg8 nm_reg8_2 (.D(Bus), .clk(Set_A), .reset(Reset), .en(Load_A), .Out(Bus), .V(A));
  RAMAsync #(.AddrBits(8), .Bits(8)) ramasync_1 (.A(A), .D(Bus), .we(Set_M), .Q(M));
  nm_enable8 nm_enable8_2 (.In(M), .en(Load_M), .Out(Bus));

  assign In = {In_7, In_6, In_5, In_4, In_3, In_2, In_1, In_0};

  // Notes on the sheet:
  //   Reset: default 1
  //   in_25: default 1
endmodule
