// Digital circuit counter_toy.dig as structural Verilog
module counter_toy (
  input  In_0,
  input  In_1,
  input  In_2,
  input  In_3,
  input  In_4,
  input  In_5,
  input  In_6,
  input  In_7,
  output [7:0] D,
  output [7:0] C
);

  wire Count_out, Load_In_out;

  Button Load_In (.out(Load_In_out));
  Button Count (.out(Count_out));
  nm_counter8 nm_counter8_1 (
    .D({In_7, In_6, In_5, In_4, In_3, In_2, In_1, In_0}), .clk(Count_out), .load(Load_In_out), .Out(C));
  LED Out_0 (.in(C[0]));
  LED Out_1 (.in(C[1]));
  LED Out_2 (.in(C[2]));
  LED Out_3 (.in(C[3]));
  LED Out_4 (.in(C[4]));
  LED Out_5 (.in(C[5]));
  LED Out_6 (.in(C[6]));
  LED Out_7 (.in(C[7]));

  assign D = {In_7, In_6, In_5, In_4, In_3, In_2, In_1, In_0};
endmodule
