// Digital circuit nc_p6.dig as structural Verilog
module nc_p6 (
  input  In_1,
  input  In_2,
  input  In_3,
  input  In_4,
  input  In_5,
  input  In_6,
  input  D,
  input  S
);

  NFET nfet_1 (.G(In_1), .D(D), .S(S));
  NFET nfet_2 (.G(In_2), .D(D), .S(S));
  NFET nfet_3 (.G(In_3), .D(D), .S(S));
  NFET nfet_4 (.G(In_4), .D(D), .S(S));
  NFET nfet_5 (.G(In_5), .D(D), .S(S));
  NFET nfet_6 (.G(In_6), .D(D), .S(S));
endmodule
