// Digital circuit nc_s2.dig as structural Verilog
module nc_s2 (
  input  In_1,
  input  In_2,
  input  D,
  input  S
);

  wire nfet_1_s;

  NFET nfet_1 (.G(In_1), .D(D), .S(nfet_1_s));
  NFET nfet_2 (.G(In_2), .D(nfet_1_s), .S(S));
endmodule
