// Digital circuit nm_ALU_FET80.dig as structural Verilog
module nm_ALU_FET80 (
  input  [7:0] X,
  input  [7:0] Y,
  input  f,
  input  c_in,
  output [7:0] Out,
  output c_out
);

  wire [7:0] nm_adder8_1_nand, nm_adder8_1_sum;

  nm_adder8 nm_adder8_1 (
    .A(X), .B(Y), .sum(nm_adder8_1_sum), .c_in(c_in), .c_out(c_out), .\nand (nm_adder8_1_nand));  // open: xor, and, nor
  nm_mux8 nm_mux8_1 (.A(nm_adder8_1_nand), .B(nm_adder8_1_sum), .s(f), .Out(Out));
endmodule
