// Digital circuit nm_adder8+.dig as structural Verilog
module nm_adder8 (
  input  [7:0] A,
  input  [7:0] B,
  input  c_in,
  output [7:0] sum,
  output c_out,
  output [7:0] \nand ,
  output [7:0] \nor ,
  output [7:0] \and ,
  output [7:0] \xor 
);

  wire nm_adder4_1_c_out;

  nm_adder4 nm_adder4_1 (
    .A(A[3:0]), .B(B[3:0]), .sum(sum[3:0]), .c_in(c_in), .c_out(nm_adder4_1_c_out), .\xor (\xor [3:0]),
    .\and (\and [3:0]), .\nor (\nor [3:0]), .\nand (\nand [3:0]));
  nm_adder4 nm_adder4_2 (
    .A(A[7:4]), .B(B[7:4]), .sum(sum[7:4]), .c_in(nm_adder4_1_c_out), .c_out(c_out), .\xor (\xor [7:4]),
    .\and (\and [7:4]), .\nor (\nor [7:4]), .\nand (\nand [7:4]));

  // Other names for the same wires on the sheet: and_0[3:0] = \and [3:0]; and_1[3:0] = \and [7:4];
  //   nand_0[3:0] = \nand [3:0]; nand_1[3:0] = \nand [7:4]; nor_0[3:0] = \nor [3:0]; nor_1[3:0] = \nor [7:4];
  //   xor_0[3:0] = \xor [3:0]; xor_1[3:0] = \xor [7:4]
endmodule
