// Digital circuit nm_and+.dig as structural Verilog
module nm_and (
  input  In_1,
  input  In_2,
  output Out,
  output Out_2
);

  nm_nand nm_nand_1 (.In_1(In_1), .In_2(In_2), .Out(Out_2));
  nm_not nm_not_1 (.In(Out_2), .Out(Out));
endmodule
