// Digital circuit nm_aoi3-3-3-3-2.dig as structural Verilog
module nm_aoi3_3_3_3_2 (
  input  In_A1,
  input  In_A2,
  input  In_B1,
  input  In_B2,
  input  In_C1,
  input  In_C2,
  input  In_D1,
  input  In_D2,
  input  In_A3,
  input  In_B3,
  input  In_C3,
  input  In_D3,
  input  In_E1,
  input  In_E2,
  output Out
);

  wire nfet_1_s, nfet_2_s, nfet_4_s, nfet_5_s, nfet_7_s, nfet_8_s, nfet_10_s, nfet_11_s, nfet_13_s;

  NFET nfet_1 (.G(In_A1), .D(Out), .S(nfet_1_s));
  NFET nfet_2 (.G(In_A2), .D(nfet_1_s), .S(nfet_2_s));
  NFET nfet_3 (.G(In_A3), .D(nfet_2_s), .S(1'b0));
  PullUp pullup_1 (.out(Out));
  NFET nfet_4 (.G(In_B1), .D(Out), .S(nfet_4_s));
  NFET nfet_5 (.G(In_B2), .D(nfet_4_s), .S(nfet_5_s));
  NFET nfet_6 (.G(In_B3), .D(nfet_5_s), .S(1'b0));
  NFET nfet_7 (.G(In_C1), .D(Out), .S(nfet_7_s));
  NFET nfet_8 (.G(In_C2), .D(nfet_7_s), .S(nfet_8_s));
  NFET nfet_9 (.G(In_C3), .D(nfet_8_s), .S(1'b0));
  NFET nfet_10 (.G(In_D1), .D(Out), .S(nfet_10_s));
  NFET nfet_11 (.G(In_D2), .D(nfet_10_s), .S(nfet_11_s));
  NFET nfet_12 (.G(In_D3), .D(nfet_11_s), .S(1'b0));
  NFET nfet_13 (.G(In_E1), .D(Out), .S(nfet_13_s));
  NFET nfet_14 (.G(In_E2), .D(nfet_13_s), .S(1'b0));
endmodule
