// Digital circuit nm_bit_resetn.dig as structural Verilog
module nm_bit_resetn (
  input  D,
  input  clk,
  input  reset,
  input  en,
  output Out,
  output V
);

  wire nm_dff_resetn_1_q_2;

  nm_dff_resetn nm_dff_resetn_1 (.D(D), .clk(clk), .r(reset), .Q(V), .Q_2(nm_dff_resetn_1_q_2));
  nm_enablen nm_enablen_1 (.In(nm_dff_resetn_1_q_2), .en(en), .Out(Out));
endmodule
