// Digital circuit nm_byte.dig as structural Verilog
module nm_byte (
  input  [7:0] D,
  input  clk,
  input  reset,
  output [7:0] Out,
  output [7:0] Out_2
);

  nm_dff nm_dff_1 (.D(D[0]), .clk(clk), .r(reset), .Q(Out[0]), .Q_2(Out_2[0]));
  nm_dff nm_dff_2 (.D(D[1]), .clk(clk), .r(reset), .Q(Out[1]), .Q_2(Out_2[1]));
  nm_dff nm_dff_3 (.D(D[2]), .clk(clk), .r(reset), .Q(Out[2]), .Q_2(Out_2[2]));
  nm_dff nm_dff_4 (.D(D[3]), .clk(clk), .r(reset), .Q(Out[3]), .Q_2(Out_2[3]));
  nm_dff nm_dff_5 (.D(D[4]), .clk(clk), .r(reset), .Q(Out[4]), .Q_2(Out_2[4]));
  nm_dff nm_dff_6 (.D(D[5]), .clk(clk), .r(reset), .Q(Out[5]), .Q_2(Out_2[5]));
  nm_dff nm_dff_7 (.D(D[6]), .clk(clk), .r(reset), .Q(Out[6]), .Q_2(Out_2[6]));
  nm_dff nm_dff_8 (.D(D[7]), .clk(clk), .r(reset), .Q(Out[7]), .Q_2(Out_2[7]));
endmodule
