// Digital circuit nm_byte2_resetn.dig as structural Verilog
module nm_byte2_resetn (
  input  [15:0] D,
  input  clk,
  input  reset,
  output [15:0] Out,
  output [15:0] Out_2
);

  nm_byte_resetn nm_byte_resetn_1 (.D(D[7:0]), .clk(clk), .reset(reset), .Out(Out[7:0]), .Out_2(Out_2[7:0]));
  nm_byte_resetn nm_byte_resetn_2 (.D(D[15:8]), .clk(clk), .reset(reset), .Out(Out[15:8]), .Out_2(Out_2[15:8]));
endmodule
