// Digital circuit nm_clock_gen.dig as structural Verilog
module nm_clock_gen (
  input  clk_i,
  input  r,
  output clk_o,
  output clk_e,
  output clk_s
);

  wire nm_tff_resetn_1_q, nm_xor_1_out;

  nm_tff_resetn nm_tff_resetn_1 (.T(clk_i), .Q(nm_tff_resetn_1_q), .r(r));  // open: Q_2
  nm_xor nm_xor_1 (.In_1(nm_tff_resetn_1_q), .In_2(clk_i), .Out(nm_xor_1_out));
  Delay delay_1 (.in(nm_tff_resetn_1_q), .out(clk_o));
  nm_or nm_or_1 (.In_1(nm_xor_1_out), .In_2(clk_o), .Out(clk_e));
  nm_and nm_and_1 (.In_1(nm_xor_1_out), .In_2(clk_o), .Out(clk_s));

  // Notes on the sheet:
  //   Clock
  //   Divider
  //   Delayed
  //   Clock
  //   Generator
  //   Mix
  //   Delayed
  //   Clock
endmodule

/* Test case:
clk_i clk_o clk_e clk_s r*
X X X X 0
0 0 0 0 1

loop(a,100)
  0 0 0 0 1
  1 1 1 0 1
  0 1 1 1 1
  1 0 1 0 1
end loop
*/
