// Digital circuit nm_conditionals.dig as structural Verilog
module nm_conditionals (
  input  zr,
  input  ng,
  output gtz,
  output gez,
  output nez,
  output ltz,
  output eqz,
  output lez
);

  nm_not nm_not_1 (.In(zr), .Out(nez));
  nm_not nm_not_2 (.In(ng), .Out(gez));
  nm_nor nm_nor_1 (.In_1(ng), .In_2(zr), .Out(gtz));
  nm_nand nm_nand_1 (.In_1(gez), .In_2(nez), .Out(lez));

  assign eqz = zr;
  assign ltz = ng;
endmodule

/* Test case:
zr ng    eqz gtz ltz   nez gez lez
0  0      0   1   0     1   1   0
1  0      1   0   0     0   1   1
0  1      0   0   1     1   0   1
*/
