// Digital circuit nm_counter16_pc.dig as structural Verilog
module nm_counter16_pc (
  input  clk,
  input  D_load,
  input  [15:0] D,
  output [15:0] Out,
  output clk_out
);

  wire nm_counter8_pc_1_clk_out;

  nm_counter8_pc nm_counter8_pc_1 (
    .clk(clk), .D(D[7:0]), .D_load(D_load), .Out(Out[7:0]), .clk_out(nm_counter8_pc_1_clk_out));
  nm_counter8_pc nm_counter8_pc_2 (
    .clk(nm_counter8_pc_1_clk_out), .D(D[15:8]), .D_load(D_load), .Out(Out[15:8]), .clk_out(clk_out));
endmodule
