// Digital circuit nm_d_gated.dig as structural Verilog
module nm_d_gated (
  input  D,
  input  E,
  output Q,
  output Q_2
);

  wire nm_nand_1_out, nm_nand_2_out;

  nm_nand nm_nand_1 (.In_1(D), .In_2(E), .Out(nm_nand_1_out));
  nm_nand nm_nand_2 (.In_1(nm_nand_1_out), .In_2(E), .Out(nm_nand_2_out));
  nm_sr nm_sr_1 (.s(nm_nand_1_out), .r(nm_nand_2_out), .Q(Q), .Q_2(Q_2));
endmodule
