// Digital circuit nm_enable8.dig as structural Verilog
module nm_enable8 (
  input  [7:0] In,
  input  en,
  output [7:0] Out
);

  wire [7:0] nm_not8x_1_out;

  nm_not8x nm_not8x_1 (.In(In), .Out(nm_not8x_1_out));
  nm_enablen8 nm_enablen8_1 (.In(nm_not8x_1_out), .en(en), .Out(Out));
endmodule
