// Digital circuit nm_enablen.dig as structural Verilog
module nm_enablen (
  input  In,
  input  en,
  output Out
);

  wire nfet_1_s, nm_not_1_out, pfet_1_d;

  nm_not nm_not_1 (.In(en), .Out(nm_not_1_out));
  PFET pfet_1 (.G(In), .S(1'b1), .D(pfet_1_d));
  PFET pfet_2 (.G(nm_not_1_out), .S(pfet_1_d), .D(Out));
  NFET nfet_1 (.G(en), .D(Out), .S(nfet_1_s));
  NFET nfet_2 (.G(In), .D(nfet_1_s), .S(1'b0));
endmodule
