// Digital circuit nm_enablen8.dig as structural Verilog
module nm_enablen8 (
  input  [7:0] In,
  input  en,
  output [7:0] Out
);

  nm_enablen nm_enablen_1 (.In(In[0]), .en(en), .Out(Out[0]));
  nm_enablen nm_enablen_2 (.In(In[1]), .en(en), .Out(Out[1]));
  nm_enablen nm_enablen_3 (.In(In[2]), .en(en), .Out(Out[2]));
  nm_enablen nm_enablen_4 (.In(In[3]), .en(en), .Out(Out[3]));
  nm_enablen nm_enablen_5 (.In(In[4]), .en(en), .Out(Out[4]));
  nm_enablen nm_enablen_6 (.In(In[5]), .en(en), .Out(Out[5]));
  nm_enablen nm_enablen_7 (.In(In[6]), .en(en), .Out(Out[6]));
  nm_enablen nm_enablen_8 (.In(In[7]), .en(en), .Out(Out[7]));
endmodule
