// Digital circuit nm_enableoc.dig as structural Verilog
module nm_enableoc (
  input  In,
  input  en,
  output Out
);

  wire nm_not_1_out;

  nm_not nm_not_1 (.In(In), .Out(nm_not_1_out));
  nm_enableocn nm_enableocn_1 (.In(nm_not_1_out), .en(en), .Out(Out));
endmodule
