// Digital circuit nm_enableocn.dig as structural Verilog
module nm_enableocn (
  input  In,
  input  en,
  output Out
);

  wire nfet_1_s;

  NFET nfet_1 (.G(In), .D(Out), .S(nfet_1_s));
  NFET nfet_2 (.G(en), .D(nfet_1_s), .S(1'b0));
endmodule
