// Digital circuit nm_invertern8.dig as structural Verilog
module nm_invertern8 (
  input  [7:0] In,
  input  inv,
  output [7:0] Out
);

  nm_xnor nm_xnor_1 (.In_1(In[0]), .In_2(inv), .Out(Out[0]));
  nm_xnor nm_xnor_2 (.In_1(In[1]), .In_2(inv), .Out(Out[1]));
  nm_xnor nm_xnor_3 (.In_1(In[2]), .In_2(inv), .Out(Out[2]));
  nm_xnor nm_xnor_4 (.In_1(In[3]), .In_2(inv), .Out(Out[3]));
  nm_xnor nm_xnor_5 (.In_1(In[4]), .In_2(inv), .Out(Out[4]));
  nm_xnor nm_xnor_6 (.In_1(In[5]), .In_2(inv), .Out(Out[5]));
  nm_xnor nm_xnor_7 (.In_1(In[6]), .In_2(inv), .Out(Out[6]));
  nm_xnor nm_xnor_8 (.In_1(In[7]), .In_2(inv), .Out(Out[7]));
endmodule
