// Digital circuit nm_mux16.dig as structural Verilog
module nm_mux16 (
  input  [15:0] A,
  input  s,
  input  [15:0] B,
  output [15:0] Out
);

  nm_mux8 nm_mux8_1 (.A(A[7:0]), .s(s), .B(B[7:0]), .Out(Out[7:0]));
  nm_mux8 nm_mux8_2 (.A(A[15:8]), .s(s), .B(B[15:8]), .Out(Out[15:8]));
endmodule
