// Digital circuit nm_mux8.dig as structural Verilog
module nm_mux8 (
  input  [7:0] A,
  input  s,
  input  [7:0] B,
  output [7:0] Out
);

  wire [7:0] nm_muxn8_1_out;

  nm_muxn8 nm_muxn8_1 (.A(A), .B(B), .s(s), .Out(nm_muxn8_1_out));
  nm_not8x nm_not8x_1 (.In(nm_muxn8_1_out), .Out(Out));
endmodule
