// Digital circuit nm_not8x.dig as structural Verilog
module nm_not8x (
  input  [7:0] In,
  output [7:0] Out
);

  nm_not nm_not_1 (.In(In[0]), .Out(Out[0]));
  nm_not nm_not_2 (.In(In[1]), .Out(Out[1]));
  nm_not nm_not_3 (.In(In[2]), .Out(Out[2]));
  nm_not nm_not_4 (.In(In[3]), .Out(Out[3]));
  nm_not nm_not_5 (.In(In[4]), .Out(Out[4]));
  nm_not nm_not_6 (.In(In[5]), .Out(Out[5]));
  nm_not nm_not_7 (.In(In[6]), .Out(Out[6]));
  nm_not nm_not_8 (.In(In[7]), .Out(Out[7]));
endmodule
