// Digital circuit nm_oai2-1.dig as structural Verilog
module nm_oai2_1 (
  input  In_A1,
  input  In_A2,
  input  In_B1,
  output Out
);

  wire nfet_1_s;

  NFET nfet_1 (.G(In_A1), .D(Out), .S(nfet_1_s));
  NFET nfet_2 (.G(In_B1), .D(nfet_1_s), .S(1'b0));
  PullUp pullup_1 (.out(Out));
  NFET nfet_3 (.G(In_A2), .D(Out), .S(nfet_1_s));
endmodule
