// Digital circuit nm_regoc8_latch.dig as structural Verilog
module nm_regoc8_latch (
  input  [7:0] D,
  input  set,
  input  en,
  output [7:0] Out,
  output [7:0] V
);

  wire [7:0] nm_byte_latch_1_out_2;

  nm_byte_latch nm_byte_latch_1 (.D(D), .set(set), .Out(V), .Out_2(nm_byte_latch_1_out_2));
  nm_enableocn8 nm_enableocn8_1 (.In(nm_byte_latch_1_out_2), .en(en), .Out(Out));
endmodule
