// Digital circuit nm_tff_clk_asyncn.dig as structural Verilog
module nm_tff_clk_asyncn (
  input  T,
  input  r,
  input  s,
  input  clk,
  output Q,
  output Q_2
);

  wire nm_aoi2_2_1_out, nm_not_1_out, nm_not_2_out;

  nm_not nm_not_1 (.In(T), .Out(nm_not_1_out));
  nm_aoi2_2 nm_aoi2_2_1 (.In_1(Q), .In_2(nm_not_1_out), .In_3(T), .In_4(Q_2), .Out(nm_aoi2_2_1_out));
  nm_not nm_not_2 (.In(nm_aoi2_2_1_out), .Out(nm_not_2_out));
  nm_dff_asyncn nm_dff_asyncn_1 (.D(nm_not_2_out), .clk(clk), .Q(Q), .Q_2(Q_2), .r(r), .s(s));
endmodule
