// Digital circuit nm_tff_clk_d.dig as structural Verilog
module nm_tff_clk_d (
  input  T,
  input  D_load,
  input  D,
  input  clk,
  output Q,
  output Q_2
);

  wire nm_nand_1_out, nm_nand_2_out, nm_not_1_out;

  nm_nand nm_nand_1 (.In_1(D), .In_2(D_load), .Out(nm_nand_1_out));
  nm_tff_clk_asyncn nm_tff_clk_asyncn_1 (.T(T), .clk(clk), .Q(Q), .Q_2(Q_2), .r(nm_nand_2_out), .s(nm_nand_1_out));
  nm_nand nm_nand_2 (.In_1(D_load), .In_2(nm_not_1_out), .Out(nm_nand_2_out));
  nm_not nm_not_1 (.In(D), .Out(nm_not_1_out));
endmodule
