// Digital circuit nm_tff_resetn.dig as structural Verilog
module nm_tff_resetn (
  input  T,
  input  r,
  output Q,
  output Q_2
);

  nm_dff_resetn nm_dff_resetn_1 (.D(Q_2), .clk(T), .Q(Q), .Q_2(Q_2), .r(r));
endmodule
