// Digital circuit nm_xor+.dig as structural Verilog
module nm_xor (
  input  In_1,
  input  In_2,
  output Out,
  output \nor 
);

  nm_nor nm_nor_1 (.In_1(In_1), .In_2(In_2), .Out(\nor ));
  nm_aoi2_1 nm_aoi2_1_1 (.In_A1(In_2), .In_A2(In_1), .In_B1(\nor ), .Out(Out));
endmodule
